// Logisim project cpu24_branch.circ as structural Verilog: 7 circuits, main circuit ◇分支相关流水线
// ALU
module MIPS_ALU (
  input  [4:0] shamt,
  input  [31:0] X,
  input  [31:0] Y,
  input  [3:0] AluOP,
  output Equal,
  output [31:0] Result,
  output [31:0] Result_2
);

  wire [0:0] comparator_1_lt, comparator_2_lt;
  wire [31:0] adder_1_out, AND_out, divider_1_out, divider_1_rem, multiplier_1_cout, multiplier_1_out,
       NOR_out, OR_out, shifter_1_out, shifter_2_out, shifter_3_out, subtractor_1_out, XOR_out;

  assign AND_out = X & Y;  // AND_Gate AND, 32 bits wide
  assign OR_out = X | Y;  // OR_Gate OR, 32 bits wide
  Shifter #(.width(32)) shifter_1 (.in(Y), .\dist (shamt), .out(shifter_1_out));
  Shifter #(.width(32), .shift("ar")) shifter_2 (.in(Y), .\dist (shamt), .out(shifter_2_out));
  Shifter #(.width(32), .shift("lr")) shifter_3 (.in(Y), .\dist (shamt), .out(shifter_3_out));
  Multiplier #(.width(32)) multiplier_1 (.a(X), .b(Y), .out(multiplier_1_out), .cout(multiplier_1_cout));  // open: cin
  Divider #(.width(32)) divider_1 (.a(X), .b(Y), .out(divider_1_out), .rem(divider_1_rem));  // open: upper
  Adder #(.width(32)) adder_1 (.a(X), .b(Y), .out(adder_1_out));  // open: cin, cout
  Subtractor #(.width(32)) subtractor_1 (.a(X), .b(Y), .out(subtractor_1_out));  // open: bin, bout
  assign XOR_out = X ^ Y;  // XOR_Gate XOR, 32 bits wide
  assign NOR_out = ~(X | Y);  // NOR_Gate NOR, 32 bits wide
  Comparator #(.width(32)) comparator_1 (.a(X), .b(Y), .eq(Equal), .lt(comparator_1_lt[0]));  // open: gt
  Comparator #(.width(32), .mode("unsigned")) comparator_2 (.a(X), .b(Y), .lt(comparator_2_lt[0]));  // open: gt, eq
  Multiplexer #(.select(4), .width(32), .enable("false")) multiplexer_1 (
    .in0(shifter_1_out), .in1(shifter_2_out), .in2(shifter_3_out), .in3(multiplier_1_out),
    .in4(divider_1_out), .in5(adder_1_out), .in6(subtractor_1_out), .in7(AND_out), .in8(OR_out),
    .in9(XOR_out), .in10(NOR_out), .in11({{31{1'b0}}, comparator_1_lt[0]}),
    .in12({{31{1'b0}}, comparator_2_lt[0]}), .in13({32{1'b0}}), .in14({32{1'b0}}), .in15({32{1'b0}}),
    .out(Result), .sel(AluOP));
  Multiplexer #(.select(4), .width(32), .enable("false")) multiplexer_2 (
    .in0({32{1'b0}}), .in1({32{1'b0}}), .in2({32{1'b0}}), .in3(multiplier_1_cout), .in4(divider_1_rem),
    .in5({32{1'b0}}), .in6({32{1'b0}}), .in7({32{1'b0}}), .in8({32{1'b0}}), .in9({32{1'b0}}),
    .in10({32{1'b0}}), .in11({32{1'b0}}), .in12({32{1'b0}}), .in13({32{1'b0}}), .in14({32{1'b0}}),
    .in15({32{1'b0}}), .out(Result_2), .sel(AluOP));

  // Other names for the same wires on the sheet: Result2[31:0] = Result_2; S[3:0] = AluOP

  // Notes on the sheet:
  //   不要改变此引脚区域内容，也不要改变ALU封装形式
  //   输入引脚
  //   输出引脚
endmodule

module MIPS_Regifile (
  input  [31:0] Din,
  input  Clk,
  input  WE,
  input  [4:0] R1_num,
  input  [4:0] W_num,
  input  [4:0] R2_num,
  output [31:0] R1,
  output [31:0] R2
);

  // RegisterFile registerfile_1: pin names not known; wires that end beside it: Din, Clk, WE, W_num, R1_num, R2_num, R1, R2
endmodule

module IF_ID (
  input  [31:0] IR,
  input  [31:0] PC,
  input  CLK,
  input  \同步清零_气泡_高电平有效 ,
  input  \使能端_低电平正常工作 ,
  output [31:0] IR_2,
  output [31:0] PC_2
);

  wire not_1_out;
  wire [31:0] multiplexer_1_out, multiplexer_2_out;

  Multiplexer #(.width(32), .enable("false")) multiplexer_1 (
    .in0(PC), .in1({32{1'b0}}), .out(multiplexer_1_out), .sel(\同步清零_气泡_高电平有效 ));
  Multiplexer #(.width(32), .enable("false")) multiplexer_2 (
    .in0(IR), .in1({32{1'b0}}), .out(multiplexer_2_out), .sel(\同步清零_气泡_高电平有效 ));
  not not_1 (not_1_out, \使能端_低电平正常工作 );
  Register #(.width(32)) register_1 (.D(multiplexer_2_out), .en(not_1_out), .Q(IR_2), .clk(CLK));  // open: clr
  Register #(.width(32)) register_2 (.D(multiplexer_1_out), .en(not_1_out), .Q(PC_2), .clk(CLK));  // open: clr
endmodule

module ID_EX (
  input  CLK,
  input  MemtoReg,
  input  RegWrite,
  input  jal,
  input  RegDst,
  input  JMP,
  input  JR,
  input  MemWrite,
  input  Syscall,
  input  [3:0] ALUOP,
  input  AluSrcB,
  input  SignExt,
  input  [31:0] IR,
  input  [31:0] PC,
  input  [31:0] A,
  input  [31:0] B,
  input  beq,
  input  bne,
  input  bgtz,
  input  lh,
  input  srlv,
  input  \同步清零_气泡_高电平有效 ,
  input  \使能端_低电平正常工作 ,
  output MemToReg_2,
  output RegWrite_2,
  output jal_2,
  output RegDst_2,
  output JMP_2,
  output JR_2,
  output MemWrite_2,
  output Syscall_2,
  output [3:0] ALUOP_2,
  output AluSrcB_2,
  output SignExt_2,
  output [31:0] IR_2,
  output [31:0] PC_2,
  output [31:0] A_2,
  output [31:0] B_2,
  output beq_2,
  output bne_2,
  output bgtz_2,
  output lh_2,
  output srlv_2
);

  wire multiplexer_1_out, multiplexer_2_out, multiplexer_3_out, multiplexer_4_out, multiplexer_5_out,
       multiplexer_6_out, multiplexer_7_out, multiplexer_8_out, multiplexer_10_out, multiplexer_11_out,
       multiplexer_16_out, multiplexer_17_out, multiplexer_18_out, multiplexer_19_out, multiplexer_20_out,
       not_1_out, undriven, undriven_2, undriven_3, undriven_4;
  wire [3:0] multiplexer_9_out;
  wire [31:0] multiplexer_12_out, multiplexer_13_out, multiplexer_14_out, multiplexer_15_out;

  Multiplexer #(.enable("false")) multiplexer_1 (
    .in0(MemtoReg), .in1(1'b0), .out(multiplexer_1_out), .sel(\同步清零_气泡_高电平有效 ));
  Multiplexer #(.enable("false")) multiplexer_2 (
    .in0(RegWrite), .in1(1'b0), .out(multiplexer_2_out), .sel(\同步清零_气泡_高电平有效 ));
  Multiplexer #(.enable("false")) multiplexer_3 (.in0(jal), .in1(1'b0), .out(multiplexer_3_out), .sel(\同步清零_气泡_高电平有效 ));
  Multiplexer #(.enable("false")) multiplexer_4 (
    .in0(RegDst), .in1(1'b0), .out(multiplexer_4_out), .sel(\同步清零_气泡_高电平有效 ));
  Multiplexer #(.enable("false")) multiplexer_5 (.in0(JMP), .in1(1'b0), .out(multiplexer_5_out), .sel(\同步清零_气泡_高电平有效 ));
  Multiplexer #(.enable("false")) multiplexer_6 (.in0(JR), .in1(1'b0), .out(multiplexer_6_out), .sel(\同步清零_气泡_高电平有效 ));
  Multiplexer #(.enable("false")) multiplexer_7 (
    .in0(MemWrite), .in1(1'b0), .out(multiplexer_7_out), .sel(\同步清零_气泡_高电平有效 ));
  Multiplexer #(.enable("false")) multiplexer_8 (
    .in0(Syscall), .in1(1'b0), .out(multiplexer_8_out), .sel(\同步清零_气泡_高电平有效 ));
  Multiplexer #(.width(4), .enable("false")) multiplexer_9 (
    .in0(ALUOP), .in1(4'b0000), .out(multiplexer_9_out), .sel(\同步清零_气泡_高电平有效 ));
  Multiplexer #(.enable("false")) multiplexer_10 (
    .in0(AluSrcB), .in1(1'b0), .out(multiplexer_10_out), .sel(\同步清零_气泡_高电平有效 ));
  Multiplexer #(.enable("false")) multiplexer_11 (
    .in0(SignExt), .in1(1'b0), .out(multiplexer_11_out), .sel(\同步清零_气泡_高电平有效 ));
  Multiplexer #(.width(32), .enable("false")) multiplexer_12 (
    .in0(IR), .in1({32{1'b0}}), .out(multiplexer_12_out), .sel(\同步清零_气泡_高电平有效 ));
  Multiplexer #(.width(32), .enable("false")) multiplexer_13 (
    .in0(PC), .in1({32{1'b0}}), .out(multiplexer_13_out), .sel(\同步清零_气泡_高电平有效 ));
  Multiplexer #(.width(32), .enable("false")) multiplexer_14 (
    .in0(A), .in1({32{1'b0}}), .out(multiplexer_14_out), .sel(\同步清零_气泡_高电平有效 ));
  Multiplexer #(.width(32), .enable("false")) multiplexer_15 (
    .in0(B), .in1({32{1'b0}}), .out(multiplexer_15_out), .sel(\同步清零_气泡_高电平有效 ));
  Multiplexer #(.enable("false")) multiplexer_16 (
    .in0(beq), .in1(1'b0), .out(multiplexer_16_out), .sel(\同步清零_气泡_高电平有效 ));
  Multiplexer #(.enable("false")) multiplexer_17 (
    .in0(bne), .in1(1'b0), .out(multiplexer_17_out), .sel(\同步清零_气泡_高电平有效 ));
  Multiplexer #(.enable("false")) multiplexer_18 (
    .in0(bgtz), .in1(1'b0), .out(multiplexer_18_out), .sel(\同步清零_气泡_高电平有效 ));
  Multiplexer #(.enable("false")) multiplexer_19 (
    .in0(lh), .in1(1'b0), .out(multiplexer_19_out), .sel(\同步清零_气泡_高电平有效 ));
  Multiplexer #(.enable("false")) multiplexer_20 (
    .in0(srlv), .in1(1'b0), .out(multiplexer_20_out), .sel(\同步清零_气泡_高电平有效 ));
  Register #(.width(1)) register_1 (.D(multiplexer_1_out), .en(not_1_out), .Q(MemToReg_2), .clk(CLK));  // open: clr
  Register #(.width(1)) register_2 (.D(multiplexer_2_out), .en(not_1_out), .Q(RegWrite_2), .clk(CLK));  // open: clr
  Register #(.width(1)) register_3 (.D(multiplexer_3_out), .en(not_1_out), .Q(jal_2), .clk(CLK));  // open: clr
  Register #(.width(1)) register_4 (.D(multiplexer_4_out), .en(not_1_out), .Q(RegDst_2), .clk(CLK));  // open: clr
  Register #(.width(1)) register_5 (.D(multiplexer_5_out), .en(not_1_out), .Q(JMP_2), .clk(CLK));  // open: clr
  Register #(.width(1)) register_6 (.D(multiplexer_6_out), .en(not_1_out), .Q(JR_2), .clk(CLK));  // open: clr
  Register #(.width(1)) register_7 (.D(multiplexer_7_out), .en(not_1_out), .Q(MemWrite_2), .clk(CLK));  // open: clr
  Register #(.width(1)) register_8 (.D(multiplexer_8_out), .en(not_1_out), .Q(Syscall_2), .clk(CLK));  // open: clr
  Register #(.width(4)) register_9 (.D(multiplexer_9_out), .en(not_1_out), .Q(ALUOP_2), .clk(CLK));  // open: clr
  Register #(.width(1)) register_10 (.D(multiplexer_10_out), .en(not_1_out), .Q(AluSrcB_2), .clk(CLK));  // open: clr
  Register #(.width(1)) register_11 (.D(multiplexer_11_out), .en(not_1_out), .Q(SignExt_2), .clk(CLK));  // open: clr
  Register #(.width(32)) register_12 (.D(multiplexer_12_out), .en(not_1_out), .Q(IR_2), .clk(CLK));  // open: clr
  Register #(.width(32)) register_13 (.D(multiplexer_13_out), .en(not_1_out), .Q(PC_2), .clk(CLK));  // open: clr
  Register #(.width(32)) register_14 (.D(multiplexer_14_out), .en(not_1_out), .Q(A_2), .clk(CLK));  // open: clr
  Register #(.width(32)) register_15 (.D(multiplexer_15_out), .en(not_1_out), .Q(B_2), .clk(CLK));  // open: clr
  Register #(.width(1)) register_16 (.D(multiplexer_16_out), .en(not_1_out), .Q(beq_2), .clk(CLK));  // open: clr
  Register #(.width(1)) register_17 (.D(multiplexer_17_out), .en(not_1_out), .Q(bne_2), .clk(CLK), .clr(undriven));
  Register #(.width(1)) register_18 (.D(multiplexer_18_out), .en(not_1_out), .Q(bgtz_2), .clk(CLK), .clr(undriven_2));
  Register #(.width(1)) register_19 (.D(multiplexer_19_out), .en(not_1_out), .Q(lh_2), .clk(CLK), .clr(undriven_3));
  Register #(.width(1)) register_20 (.D(multiplexer_20_out), .en(not_1_out), .Q(srlv_2), .clk(CLK), .clr(undriven_4));
  not not_1 (not_1_out, \使能端_低电平正常工作 );
endmodule

module EX_MEM (
  input  CLK,
  input  MemtoReg,
  input  RegWrite,
  input  jal,
  input  RegDst,
  input  lh,
  input  MemWrite,
  input  pause,
  input  [31:0] IR,
  input  [31:0] PC,
  input  [31:0] ALU_Result,
  input  [31:0] B,
  input  \同步清零_气泡_高电平有效 ,
  input  \使能端_低电平正常工作 ,
  output MemToReg_2,
  output RegWrite_2,
  output jal_2,
  output RegDst_2,
  output lh_2,
  output MemWrite_2,
  output pause_2,
  output [31:0] IR_2,
  output [31:0] PC_2,
  output [31:0] ALU_Result_2,
  output [31:0] B_2
);

  wire multiplexer_1_out, multiplexer_2_out, multiplexer_3_out, multiplexer_4_out, multiplexer_5_out,
       multiplexer_6_out, multiplexer_7_out, not_1_out;
  wire [31:0] multiplexer_8_out, multiplexer_9_out, multiplexer_10_out, multiplexer_11_out;

  Multiplexer #(.enable("false")) multiplexer_1 (
    .in0(MemtoReg), .in1(1'b0), .out(multiplexer_1_out), .sel(\同步清零_气泡_高电平有效 ));
  Multiplexer #(.enable("false")) multiplexer_2 (
    .in0(RegWrite), .in1(1'b0), .out(multiplexer_2_out), .sel(\同步清零_气泡_高电平有效 ));
  Multiplexer #(.enable("false")) multiplexer_3 (.in0(jal), .in1(1'b0), .out(multiplexer_3_out), .sel(\同步清零_气泡_高电平有效 ));
  Multiplexer #(.enable("false")) multiplexer_4 (
    .in0(RegDst), .in1(1'b0), .out(multiplexer_4_out), .sel(\同步清零_气泡_高电平有效 ));
  Multiplexer #(.enable("false")) multiplexer_5 (.in0(lh), .in1(1'b0), .out(multiplexer_5_out), .sel(\同步清零_气泡_高电平有效 ));
  Multiplexer #(.enable("false")) multiplexer_6 (
    .in0(MemWrite), .in1(1'b0), .out(multiplexer_6_out), .sel(\同步清零_气泡_高电平有效 ));
  Multiplexer #(.enable("false")) multiplexer_7 (
    .in0(pause), .in1(1'b0), .out(multiplexer_7_out), .sel(\同步清零_气泡_高电平有效 ));
  Multiplexer #(.width(32), .enable("false")) multiplexer_8 (
    .in0(IR), .in1({32{1'b0}}), .out(multiplexer_8_out), .sel(\同步清零_气泡_高电平有效 ));
  Multiplexer #(.width(32), .enable("false")) multiplexer_9 (
    .in0(PC), .in1({32{1'b0}}), .out(multiplexer_9_out), .sel(\同步清零_气泡_高电平有效 ));
  Multiplexer #(.width(32), .enable("false")) multiplexer_10 (
    .in0(ALU_Result), .in1({32{1'b0}}), .out(multiplexer_10_out), .sel(\同步清零_气泡_高电平有效 ));
  Multiplexer #(.width(32), .enable("false")) multiplexer_11 (
    .in0(B), .in1({32{1'b0}}), .out(multiplexer_11_out), .sel(\同步清零_气泡_高电平有效 ));
  Register #(.width(1)) register_1 (.D(multiplexer_1_out), .en(not_1_out), .Q(MemToReg_2), .clk(CLK), .clr(1'b0));
  Register #(.width(1)) register_2 (.D(multiplexer_2_out), .en(not_1_out), .Q(RegWrite_2), .clk(CLK), .clr(1'b0));
  Register #(.width(1)) register_3 (.D(multiplexer_3_out), .en(not_1_out), .Q(jal_2), .clk(CLK), .clr(1'b0));
  Register #(.width(1)) register_4 (.D(multiplexer_4_out), .en(not_1_out), .Q(RegDst_2), .clk(CLK), .clr(1'b0));
  Register #(.width(1)) register_5 (.D(multiplexer_5_out), .en(not_1_out), .Q(lh_2), .clk(CLK), .clr(1'b0));
  Register #(.width(1)) register_6 (.D(multiplexer_6_out), .en(not_1_out), .Q(MemWrite_2), .clk(CLK), .clr(1'b0));
  Register #(.width(1)) register_7 (.D(multiplexer_7_out), .en(not_1_out), .Q(pause_2), .clk(CLK), .clr(1'b0));
  Register #(.width(32)) register_8 (.D(multiplexer_8_out), .en(not_1_out), .Q(IR_2), .clk(CLK), .clr(1'b0));
  Register #(.width(32)) register_9 (.D(multiplexer_9_out), .en(not_1_out), .Q(PC_2), .clk(CLK), .clr(1'b0));
  Register #(.width(32)) register_10 (.D(multiplexer_10_out), .en(not_1_out), .Q(ALU_Result_2), .clk(CLK), .clr(1'b0));
  Register #(.width(32)) register_11 (.D(multiplexer_11_out), .en(not_1_out), .Q(B_2), .clk(CLK), .clr(1'b0));
  not not_1 (not_1_out, \使能端_低电平正常工作 );
endmodule

module MEM_WB (
  input  CLK,
  input  MemtoReg,
  input  RegWrite,
  input  jal,
  input  RegDst,
  input  pause,
  input  [31:0] IR,
  input  [31:0] PC,
  input  [31:0] ALU_Result,
  input  [31:0] Dout,
  input  \同步清零_气泡_高电平有效 ,
  input  \使能端_低电平正常工作 ,
  output MemToReg_2,
  output RegWrite_2,
  output jal_2,
  output RegDst_2,
  output pause_2,
  output [31:0] IR_2,
  output [31:0] PC_2,
  output [31:0] ALU_Result_2,
  output [31:0] Dout_2
);

  wire multiplexer_1_out, multiplexer_2_out, multiplexer_3_out, multiplexer_4_out, multiplexer_5_out,
       not_1_out;
  wire [31:0] multiplexer_6_out, multiplexer_7_out, multiplexer_8_out, multiplexer_9_out;

  Multiplexer #(.enable("false")) multiplexer_1 (
    .in0(MemtoReg), .in1(1'b0), .out(multiplexer_1_out), .sel(\同步清零_气泡_高电平有效 ));
  Multiplexer #(.enable("false")) multiplexer_2 (
    .in0(RegWrite), .in1(1'b0), .out(multiplexer_2_out), .sel(\同步清零_气泡_高电平有效 ));
  Multiplexer #(.enable("false")) multiplexer_3 (.in0(jal), .in1(1'b0), .out(multiplexer_3_out), .sel(\同步清零_气泡_高电平有效 ));
  Multiplexer #(.enable("false")) multiplexer_4 (
    .in0(RegDst), .in1(1'b0), .out(multiplexer_4_out), .sel(\同步清零_气泡_高电平有效 ));
  Multiplexer #(.enable("false")) multiplexer_5 (
    .in0(pause), .in1(1'b0), .out(multiplexer_5_out), .sel(\同步清零_气泡_高电平有效 ));
  Multiplexer #(.width(32), .enable("false")) multiplexer_6 (
    .in0(IR), .in1({32{1'b0}}), .out(multiplexer_6_out), .sel(\同步清零_气泡_高电平有效 ));
  Multiplexer #(.width(32), .enable("false")) multiplexer_7 (
    .in0(PC), .in1({32{1'b0}}), .out(multiplexer_7_out), .sel(\同步清零_气泡_高电平有效 ));
  Multiplexer #(.width(32), .enable("false")) multiplexer_8 (
    .in0(ALU_Result), .in1({32{1'b0}}), .out(multiplexer_8_out), .sel(\同步清零_气泡_高电平有效 ));
  Multiplexer #(.width(32), .enable("false")) multiplexer_9 (
    .in0(Dout), .in1({32{1'b0}}), .out(multiplexer_9_out), .sel(\同步清零_气泡_高电平有效 ));
  Register #(.width(1)) register_1 (.D(multiplexer_1_out), .en(not_1_out), .Q(MemToReg_2), .clk(CLK), .clr(1'b0));
  Register #(.width(1)) register_2 (.D(multiplexer_2_out), .en(not_1_out), .Q(RegWrite_2), .clk(CLK), .clr(1'b0));
  Register #(.width(1)) register_3 (.D(multiplexer_3_out), .en(not_1_out), .Q(jal_2), .clk(CLK), .clr(1'b0));
  Register #(.width(1)) register_4 (.D(multiplexer_4_out), .en(not_1_out), .Q(RegDst_2), .clk(CLK), .clr(1'b0));
  Register #(.width(1)) register_5 (.D(multiplexer_5_out), .en(not_1_out), .Q(pause_2), .clk(CLK), .clr(1'b0));
  Register #(.width(32)) register_6 (.D(multiplexer_6_out), .en(not_1_out), .Q(IR_2), .clk(CLK), .clr(1'b0));
  Register #(.width(32)) register_7 (.D(multiplexer_7_out), .en(not_1_out), .Q(PC_2), .clk(CLK), .clr(1'b0));
  Register #(.width(32)) register_8 (.D(multiplexer_8_out), .en(not_1_out), .Q(ALU_Result_2), .clk(CLK), .clr(1'b0));
  Register #(.width(32)) register_9 (.D(multiplexer_9_out), .en(not_1_out), .Q(Dout_2), .clk(CLK), .clr(1'b0));
  not not_1 (not_1_out, \使能端_低电平正常工作 );
endmodule

module \分支相关流水线  (
);

  wire AluSrcB, and_1_out, and_2_out, and_3_out, and_4_out, and_5_out, and_6_out, and_7_out, and_8_out, BGTZ,
       bgtz_ex, branch, bubble, CLK, comparator_1_eq, ex_mem_1_jal_2, ex_mem_1_memtoreg_2,
       ex_mem_1_memwrite_2, ex_mem_1_pause_2, ex_mem_1_regdst_2, ex_mem_1_regwrite_2, Go, id_ex_1_beq_2,
       id_ex_1_bne_2, id_ex_1_jal_2, id_ex_1_lh_2, id_ex_1_memtoreg_2, id_ex_1_memwrite_2, id_ex_1_regdst_2,
       id_ex_1_regwrite_2, id_ex_1_srlv_2, IR1, IR2, IR3, jal, JMP, JR, LH, LH_MEM, mem_wb_1_memtoreg_2,
       mips_ram_1_p10, nor_1_out, not_1_out, not_2_out, or_1_out, or_4_out, pause, regdst, RST, sel,
       SignedExt, SRLV, syscall, syscall_ex, W1, W2, W3, wb_pause, WB_RegWrite, \硬布线控制器_1_alu_src ,
       \硬布线控制器_1_beq , \硬布线控制器_1_bne , \硬布线控制器_1_jal , \硬布线控制器_1_jmp , \硬布线控制器_1_jr , \硬布线控制器_1_memtoreg ,
       \硬布线控制器_1_memwrite , \硬布线控制器_1_regdst , \硬布线控制器_1_regwrite , \硬布线控制器_1_signedext ;
  wire [3:0] id_ex_1_aluop_2, \硬布线控制器_1_alu_op ;
  wire [4:0] multiplexer_1_out, multiplexer_2_out, multiplexer_3_out, W_num;
  wire [9:0] ex_mem_1_alu_result_2_2;
  wire [15:0] imme, \LoadUse次数 , wb_imme, \总周期数 , \插入气泡数 , \无条件分支数 , \条件分支成功数 ;
  wire [21:0] ex_mem_1_alu_result_2;
  wire [25:16] instr_index;
  wire [31:0] adder_1_out, adder_2_out, adder_3_out, adder_4_out, B, bit_extender_1_out, bit_extender_2_out,
       bit_extender_3_out, bit_extender_4_out, bit_extender_5_out, controlled_buffer_7_out, ex_mem_1_b_2,
       ex_mem_1_ir_2, EX_PC, ID_PC, if_id_1_ir_2, IF_PC, LedData, MEM_PC, mem_wb_1_alu_result_2,
       mem_wb_1_dout_2, mips_alu_1_result, mips_regifile_1_r1, mips_regifile_1_r2, multiplexer_4_out,
       multiplexer_5_out, multiplexer_6_out, PC, R1, R2, Reg_din, rom_1_data, undriven, WB_PC;
  wire [31:16] mem_wb_1_ir_2;
  wire [31:26] id_ex_1_ir_2;

  Button \u_总复位  (.out(RST));
  Button _1 (.out(IR1));
  Button _2 (.out(IR2));
  Button _3 (.out(IR3));
  not not_1 (not_1_out, wb_pause);
  Button \u_继续运行  (.out(Go));
  LED led_1 (.in(W1));
  LED led_2 (.in(W2));
  LED led_3 (.in(W3));
  Register #(.width(32)) u_PC (.D(PC), .en(not_1_out), .Q(IF_PC), .clk(CLK), .clr(RST));
  Hex_Digit_Display hex_digit_display_1 (.value(LedData[31:28]));  // open: dp
  and and_1 (and_1_out, not_1_out, JMP);
  and and_2 (and_2_out, not_1_out, branch);
  Hex_Digit_Display hex_digit_display_2 (.value(LedData[27:24]));  // open: dp
  Hex_Digit_Display hex_digit_display_3 (.value(LedData[23:20]));  // open: dp
  Counter #(.width(16), .max('hffff)) counter_1 (
    .count(and_1_out), .Q(\无条件分支数 ), .clk(CLK), .clr(RST));  // open: load, D, carry
  Counter #(.width(16), .max('hffff)) counter_2 (
    .count(not_1_out), .Q(\总周期数 ), .clk(CLK), .clr(RST));  // open: load, D, carry
  Counter #(.width(16), .max('hffff)) counter_3 (
    .count(and_2_out), .Q(\条件分支成功数 ), .clk(CLK), .clr(RST));  // open: load, D, carry
  Hex_Digit_Display hex_digit_display_4 (.value(LedData[19:16]));  // open: dp
  Hex_Digit_Display hex_digit_display_5 (.value(LedData[15:12]));  // open: dp
  or or_1 (or_1_out, bubble, RST);
  IF_ID if_id_1 (
    .IR(rom_1_data), .PC(IF_PC), .IR_2(if_id_1_ir_2), .PC_2(ID_PC), .CLK(CLK), .\使能端_低电平正常工作 (wb_pause),
    .\同步清零_气泡_高电平有效 (or_1_out));
  ROM #(.addrWidth(10), .dataWidth(32)) rom_1 (.addr(IF_PC[11:2]), .data(rom_1_data));  // open: sel
  Hex_Digit_Display hex_digit_display_6 (.value(LedData[11:8]));  // open: dp
  Hex_Digit_Display hex_digit_display_7 (.value(LedData[7:4]));  // open: dp
  Clock clock_1 (.out(CLK));
  Hex_Digit_Display hex_digit_display_8 (.value(LedData[3:0]));  // open: dp
  Multiplexer #(.width(5), .enable("false")) multiplexer_1 (
    .in0(if_id_1_ir_2[25:21]), .in1(5'b00010), .out(multiplexer_1_out), .sel(syscall));
  Multiplexer #(.width(5), .enable("false")) multiplexer_2 (
    .in0(if_id_1_ir_2[20:16]), .in1(5'b00100), .out(multiplexer_2_out), .sel(syscall));
  \硬布线控制器  \u_硬布线控制器_1  (
    .Func(if_id_1_ir_2[5:0]), .OP(if_id_1_ir_2[31:26]), .ALU_OP(\硬布线控制器_1_alu_op ),
    .MemToReg(\硬布线控制器_1_memtoreg ), .MemWrite(\硬布线控制器_1_memwrite ), .ALU_SRC(\硬布线控制器_1_alu_src ),
    .RegWrite(\硬布线控制器_1_regwrite ), .SysCALL(syscall), .SignedExt(\硬布线控制器_1_signedext ),
    .RegDst(\硬布线控制器_1_regdst ), .JR(\硬布线控制器_1_jr ), .JMP(\硬布线控制器_1_jmp ), .Beq(\硬布线控制器_1_beq ),
    .JAL(\硬布线控制器_1_jal ), .Bne(\硬布线控制器_1_bne ), .BGTZ(BGTZ), .LH(LH), .SRLV(SRLV));
  // Probe on \总周期数 
  // Probe on \无条件分支数 
  // Probe on \条件分支成功数 
  // Probe on \插入气泡数 
  // Probe on \LoadUse次数 
  ID_EX id_ex_1 (
    .MemtoReg(\硬布线控制器_1_memtoreg ), .RegWrite(\硬布线控制器_1_regwrite ), .jal(\硬布线控制器_1_jal ), .CLK(CLK),
    .RegDst(\硬布线控制器_1_regdst ), .JMP(\硬布线控制器_1_jmp ), .JR(\硬布线控制器_1_jr ), .MemWrite(\硬布线控制器_1_memwrite ),
    .Syscall(syscall), .ALUOP(\硬布线控制器_1_alu_op ), .AluSrcB(\硬布线控制器_1_alu_src ),
    .SignExt(\硬布线控制器_1_signedext ), .IR(if_id_1_ir_2), .PC(ID_PC), .A(mips_regifile_1_r1),
    .B(mips_regifile_1_r2), .MemToReg_2(id_ex_1_memtoreg_2), .RegWrite_2(id_ex_1_regwrite_2),
    .jal_2(id_ex_1_jal_2), .RegDst_2(id_ex_1_regdst_2), .JMP_2(JMP), .JR_2(JR),
    .MemWrite_2(id_ex_1_memwrite_2), .Syscall_2(syscall_ex), .ALUOP_2(id_ex_1_aluop_2), .AluSrcB_2(AluSrcB),
    .SignExt_2(SignedExt), .IR_2({id_ex_1_ir_2, instr_index, imme}), .PC_2(EX_PC), .A_2(R1), .B_2(R2),
    .\使能端_低电平正常工作 (wb_pause), .\同步清零_气泡_高电平有效 (or_1_out), .beq(\硬布线控制器_1_beq ), .bne(\硬布线控制器_1_bne ),
    .beq_2(id_ex_1_beq_2), .bne_2(id_ex_1_bne_2), .bgtz(BGTZ), .bgtz_2(bgtz_ex), .lh(LH),
    .lh_2(id_ex_1_lh_2), .srlv(SRLV), .srlv_2(id_ex_1_srlv_2));
  MIPS_Regifile mips_regifile_1 (
    .Din(Reg_din), .Clk(CLK), .R1(mips_regifile_1_r1), .R2(mips_regifile_1_r2), .WE(WB_RegWrite),
    .W_num(W_num), .R1_num(multiplexer_1_out), .R2_num(multiplexer_2_out));
  Adder #(.width(32)) adder_1 (.a(32'h4), .b(EX_PC), .out(adder_1_out));  // open: cin, cout
  // Probe on IF_PC[11:0]
  Multiplexer #(.width(5), .enable("false")) multiplexer_3 (
    .in0(imme[10:6]), .in1(R1[4:0]), .out(multiplexer_3_out), .sel(id_ex_1_srlv_2));
  Comparator #(.width(32), .mode("unsigned")) comparator_1 (
    .a({32{1'b0}}), .b(R1), .eq(comparator_1_eq));  // open: gt, lt
  assign bit_extender_1_out = {{16{imme[15]}}, imme};  // Bit_Extender bit_extender_1
  assign bit_extender_2_out = {{16{1'b0}}, imme};  // Bit_Extender bit_extender_2
  assign B = and_3_out ? R2 : 32'bz;  // Controlled_Buffer controlled_buffer_1
  and and_3 (and_3_out, ~syscall_ex, ~AluSrcB);  // AND_Gate
  Register #(.width(32)) register_1 (.D(R2), .en(and_4_out), .Q(LedData), .clk(CLK));  // open: clr
  and and_4 (and_4_out, sel, syscall_ex);
  // Probe on ID_PC[11:0]
  and and_5 (and_5_out, id_ex_1_beq_2, sel);
  and and_6 (and_6_out, ~sel, id_ex_1_bne_2);  // AND_Gate
  MIPS_ALU mips_alu_1 (
    .X(R1), .Y(B), .AluOP(id_ex_1_aluop_2), .Equal(sel), .Result(mips_alu_1_result), .shamt(multiplexer_3_out));  // open: Result_2
  and and_7 (and_7_out, bgtz_ex, ~R1[31], ~comparator_1_eq);  // AND_Gate
  assign B = syscall_ex ? 32'h22 : 32'bz;  // Controlled_Buffer controlled_buffer_2
  assign B = SignedExt ? bit_extender_1_out : 32'bz;  // Controlled_Buffer controlled_buffer_3
  assign B = and_8_out ? bit_extender_2_out : 32'bz;  // Controlled_Buffer controlled_buffer_4
  and and_8 (and_8_out, AluSrcB, ~SignedExt);  // AND_Gate
  assign bit_extender_3_out = {{14{imme[15]}}, {imme, 2'b00}};  // Bit_Extender bit_extender_3
  and and_9 (pause, ~sel, syscall_ex);  // AND_Gate
  // Probe on EX_PC[11:0]
  // Probe on MEM_PC[11:0]
  or or_2 (branch, and_5_out, and_7_out, and_6_out);
  Adder #(.width(32)) adder_2 (.a(adder_1_out), .b(bit_extender_3_out), .out(adder_2_out));  // open: cin, cout
  Adder #(.width(32)) adder_3 (.a(32'h4), .b(IF_PC), .out(adder_3_out));  // open: cin, cout
  Multiplexer #(.width(32), .enable("false")) multiplexer_4 (
    .in0({adder_1_out[31:28], instr_index, imme, 2'b00}), .in1(R1), .out(multiplexer_4_out), .sel(JR));
  // Probe on WB_PC[11:0]
  EX_MEM ex_mem_1 (
    .MemtoReg(id_ex_1_memtoreg_2), .RegWrite(id_ex_1_regwrite_2), .jal(id_ex_1_jal_2), .CLK(CLK),
    .RegDst(id_ex_1_regdst_2), .lh(id_ex_1_lh_2), .MemWrite(id_ex_1_memwrite_2), .pause(pause),
    .IR({id_ex_1_ir_2, instr_index, imme}), .PC(EX_PC), .ALU_Result(mips_alu_1_result),
    .MemToReg_2(ex_mem_1_memtoreg_2), .RegWrite_2(ex_mem_1_regwrite_2), .jal_2(ex_mem_1_jal_2),
    .RegDst_2(ex_mem_1_regdst_2), .lh_2(LH_MEM), .MemWrite_2(ex_mem_1_memwrite_2),
    .pause_2(ex_mem_1_pause_2), .IR_2(ex_mem_1_ir_2), .PC_2(MEM_PC),
    .ALU_Result_2({ex_mem_1_alu_result_2_2, ex_mem_1_alu_result_2}), .\使能端_低电平正常工作 (wb_pause), .B(R2),
    .B_2(ex_mem_1_b_2), .\同步清零_气泡_高电平有效 (RST));
  Multiplexer #(.width(32), .enable("false")) multiplexer_5 (
    .in0(adder_3_out), .in1(adder_2_out), .out(multiplexer_5_out), .sel(branch));
  assign PC = JMP ? multiplexer_4_out : 32'bz;  // Controlled_Buffer controlled_buffer_5
  or or_3 (bubble, JR, branch, JMP);
  assign PC = not_2_out ? multiplexer_5_out : 32'bz;  // Controlled_Buffer controlled_buffer_6
  not not_2 (not_2_out, JMP);
  or or_4 (or_4_out, ex_mem_1_memtoreg_2, LH_MEM);
  MEM_WB mem_wb_1 (
    .MemtoReg(ex_mem_1_memtoreg_2), .RegWrite(ex_mem_1_regwrite_2), .jal(ex_mem_1_jal_2), .CLK(CLK),
    .RegDst(ex_mem_1_regdst_2), .pause(ex_mem_1_pause_2), .IR(ex_mem_1_ir_2), .PC(MEM_PC),
    .ALU_Result({ex_mem_1_alu_result_2_2, ex_mem_1_alu_result_2}), .MemToReg_2(mem_wb_1_memtoreg_2),
    .RegWrite_2(WB_RegWrite), .jal_2(jal), .RegDst_2(regdst), .pause_2(wb_pause),
    .IR_2({mem_wb_1_ir_2, wb_imme}), .PC_2(WB_PC), .ALU_Result_2(mem_wb_1_alu_result_2),
    .Dout(controlled_buffer_7_out), .Dout_2(mem_wb_1_dout_2), .\同步清零_气泡_高电平有效 (RST), .\使能端_低电平正常工作 (wb_pause));
  // MIPS_RAM mips_ram_1: pin names not known; wires that end beside it: branch, R1, ex_mem_1_alu_result_2, ex_mem_1_alu_result_2[21:2], ex_mem_1_b_2, ex_mem_1_memwrite_2, CLK, or_4_out, RST, mips_ram_1_p10, mips_ram_1_p10
  assign controlled_buffer_7_out = ex_mem_1_memtoreg_2 ? undriven : 32'bz;  // Controlled_Buffer controlled_buffer_7
  assign bit_extender_4_out = {{16{undriven[15]}}, undriven[15:0]};  // Bit_Extender bit_extender_4
  Multiplexer #(.width(32), .enable("false")) multiplexer_6 (
    .in0(bit_extender_4_out), .in1(bit_extender_5_out), .out(multiplexer_6_out),
    .sel(ex_mem_1_alu_result_2[1]));
  assign bit_extender_5_out = {{16{undriven[31]}}, undriven[31:16]};  // Bit_Extender bit_extender_5
  assign controlled_buffer_7_out = LH_MEM ? multiplexer_6_out : 32'bz;  // Controlled_Buffer controlled_buffer_8
  Adder #(.width(32)) adder_4 (.a(32'h4), .b(WB_PC), .out(adder_4_out));  // open: cin, cout
  assign Reg_din = mem_wb_1_memtoreg_2 ? mem_wb_1_dout_2 : 32'bz;  // Controlled_Buffer controlled_buffer_9
  Multiplexer #(.select(2), .width(5), .enable("false")) multiplexer_7 (
    .in0(mem_wb_1_ir_2[20:16]), .in1({5{1'b1}}), .in2(wb_imme[15:11]), .out(W_num), .sel({regdst, jal}));  // open: in3
  nor nor_1 (nor_1_out, mem_wb_1_memtoreg_2, jal);
  assign Reg_din = jal ? adder_4_out : 32'bz;  // Controlled_Buffer controlled_buffer_10
  assign Reg_din = nor_1_out ? mem_wb_1_alu_result_2 : 32'bz;  // Controlled_Buffer controlled_buffer_11

  // Other names for the same wires on the sheet: instr_index[15:0] = imme; shamt[4:0] = imme[10:6]

  // Notes on the sheet:
  //   中断源
  //   中断等待指示
  //   指令存储器
  //   数码管输出
  //   contents of rom_1 (hex, n*v repeats v):
  //   20110020 20020022 8000c06 20110004 20120005 20130006 10000003 20110007 20120008 20130009 14110003
  //   2011000a 2012000b 2013000c c000c14 2002000a 0 0 0 c 2231ffff 0 0 0 112020 0 0 0 c 1620fff6 3e00008
  //   Func
  //   rs
  //   rt
  //   流水调试日志用
  //   ins_ind
  //   rd
  //   rt
endmodule
