// Logisim project cpu24_redirect _bht.circ as structural Verilog: 11 circuits, main circuit ◆MIPS ALU
// ALU
module MIPS_ALU (
  input  [4:0] shamt,
  input  [31:0] X,
  input  [31:0] Y,
  input  [3:0] AluOP,
  output Equal,
  output [31:0] Result,
  output [31:0] Result_2
);

  wire [0:0] comparator_1_lt, comparator_2_lt;
  wire [31:0] adder_1_out, AND_out, divider_1_out, divider_1_rem, multiplier_1_cout, multiplier_1_out,
       NOR_out, OR_out, shifter_1_out, shifter_2_out, shifter_3_out, subtractor_1_out, XOR_out;

  assign AND_out = X & Y;  // AND_Gate AND, 32 bits wide
  assign OR_out = X | Y;  // OR_Gate OR, 32 bits wide
  Shifter #(.width(32)) shifter_1 (.in(Y), .\dist (shamt), .out(shifter_1_out));
  Shifter #(.width(32), .shift("ar")) shifter_2 (.in(Y), .\dist (shamt), .out(shifter_2_out));
  Shifter #(.width(32), .shift("lr")) shifter_3 (.in(Y), .\dist (shamt), .out(shifter_3_out));
  Multiplier #(.width(32)) multiplier_1 (.a(X), .b(Y), .out(multiplier_1_out), .cout(multiplier_1_cout));  // open: cin
  Divider #(.width(32)) divider_1 (.a(X), .b(Y), .out(divider_1_out), .rem(divider_1_rem));  // open: upper
  Adder #(.width(32)) adder_1 (.a(X), .b(Y), .out(adder_1_out));  // open: cin, cout
  Subtractor #(.width(32)) subtractor_1 (.a(X), .b(Y), .out(subtractor_1_out));  // open: bin, bout
  assign XOR_out = X ^ Y;  // XOR_Gate XOR, 32 bits wide
  assign NOR_out = ~(X | Y);  // NOR_Gate NOR, 32 bits wide
  Comparator #(.width(32)) comparator_1 (.a(X), .b(Y), .eq(Equal), .lt(comparator_1_lt[0]));  // open: gt
  Comparator #(.width(32), .mode("unsigned")) comparator_2 (.a(X), .b(Y), .lt(comparator_2_lt[0]));  // open: gt, eq
  Multiplexer #(.select(4), .width(32), .enable("false")) multiplexer_1 (
    .in0(shifter_1_out), .in1(shifter_2_out), .in2(shifter_3_out), .in3(multiplier_1_out),
    .in4(divider_1_out), .in5(adder_1_out), .in6(subtractor_1_out), .in7(AND_out), .in8(OR_out),
    .in9(XOR_out), .in10(NOR_out), .in11({{31{1'b0}}, comparator_1_lt[0]}),
    .in12({{31{1'b0}}, comparator_2_lt[0]}), .in13({32{1'b0}}), .in14({32{1'b0}}), .in15({32{1'b0}}),
    .out(Result), .sel(AluOP));
  Multiplexer #(.select(4), .width(32), .enable("false")) multiplexer_2 (
    .in0({32{1'b0}}), .in1({32{1'b0}}), .in2({32{1'b0}}), .in3(multiplier_1_cout), .in4(divider_1_rem),
    .in5({32{1'b0}}), .in6({32{1'b0}}), .in7({32{1'b0}}), .in8({32{1'b0}}), .in9({32{1'b0}}),
    .in10({32{1'b0}}), .in11({32{1'b0}}), .in12({32{1'b0}}), .in13({32{1'b0}}), .in14({32{1'b0}}),
    .in15({32{1'b0}}), .out(Result_2), .sel(AluOP));

  // Other names for the same wires on the sheet: Result2[31:0] = Result_2; S[3:0] = AluOP

  // Notes on the sheet:
  //   不要改变此引脚区域内容，也不要改变ALU封装形式
  //   输入引脚
  //   输出引脚
endmodule

module MIPS_Regifile (
  input  [31:0] Din,
  input  Clk,
  input  WE,
  input  [4:0] R1_num,
  input  [4:0] W_num,
  input  [4:0] R2_num,
  output [31:0] R1,
  output [31:0] R2
);

  // RegisterFile registerfile_1: pin names not known; wires that end beside it: Din, Clk, WE, W_num, R1_num, R2_num, R1, R2
endmodule

// 源寄存器使用情况
module \源寄存器使用情况  (
  input  OP0,
  input  OP1,
  input  OP2,
  input  OP3,
  input  OP4,
  input  OP5,
  input  F0,
  input  F1,
  input  F2,
  input  F3,
  input  F4,
  input  F5,
  output R1_Used,
  output R2_Used
);

  wire and_1_out, and_2_out, and_3_out, and_4_out, and_5_out, and_6_out, and_7_out, and_8_out, and_9_out,
       and_10_out, and_11_out, and_12_out, and_13_out, and_14_out, and_15_out, and_16_out, and_17_out,
       and_18_out, and_19_out, and_20_out, and_21_out, and_22_out, and_23_out, and_24_out, and_25_out,
       and_26_out, and_27_out, and_28_out, and_29_out, and_30_out, and_31_out, and_32_out, and_33_out,
       and_34_out, and_35_out, and_36_out, and_37_out, and_38_out, and_39_out, not_1_out, not_2_out,
       not_3_out, not_4_out, not_5_out, not_6_out, not_7_out, not_8_out, not_9_out, not_10_out, not_11_out,
       not_12_out, not_13_out, not_14_out, not_15_out, not_16_out, not_17_out, not_18_out, not_19_out,
       not_20_out, not_21_out, not_22_out, not_23_out, not_24_out, not_25_out, not_26_out, not_27_out,
       not_28_out, not_29_out, not_30_out, not_31_out, not_32_out, not_33_out, not_34_out, not_35_out,
       not_36_out, not_37_out, not_38_out, not_39_out, not_40_out, not_41_out, not_42_out, not_43_out,
       not_44_out, not_45_out, not_46_out, not_47_out, not_48_out, not_49_out, not_50_out, not_51_out,
       not_52_out, not_53_out, not_54_out, not_55_out, not_56_out, not_57_out, not_58_out, not_59_out,
       not_60_out, not_61_out, not_62_out, not_63_out, not_64_out, not_65_out, not_66_out, not_67_out,
       not_68_out, not_69_out, not_70_out, not_71_out, not_72_out, not_73_out, not_74_out, not_75_out,
       not_76_out, not_77_out, not_78_out, not_79_out, not_80_out, not_81_out, not_82_out, not_83_out,
       not_84_out, not_85_out, not_86_out, not_87_out, not_88_out, not_89_out, not_90_out, not_91_out,
       not_92_out, not_93_out, not_94_out, not_95_out, not_96_out, not_97_out, not_98_out, not_99_out,
       not_100_out, not_101_out, not_102_out, not_103_out, not_104_out, not_105_out, not_106_out,
       not_107_out, not_108_out, not_109_out, not_110_out, not_111_out, not_112_out, not_113_out,
       not_114_out, not_115_out, not_116_out, not_117_out, not_118_out, not_119_out, not_120_out,
       not_121_out, not_122_out, not_123_out, not_124_out, not_125_out, not_126_out, not_127_out,
       not_128_out, not_129_out, not_130_out, not_131_out, not_132_out, not_133_out, not_134_out,
       not_135_out, not_136_out, not_137_out, not_138_out, not_139_out, not_140_out, not_141_out,
       not_142_out, not_143_out, not_144_out, not_145_out, not_146_out, not_147_out, not_148_out,
       not_149_out, not_150_out, not_151_out, not_152_out, not_153_out, not_154_out, not_155_out,
       not_156_out, not_157_out, not_158_out, not_159_out, not_160_out, not_161_out, not_162_out,
       not_163_out, not_164_out, not_165_out, not_166_out, not_167_out, not_168_out, not_169_out,
       not_170_out, not_171_out, not_172_out, not_173_out, not_174_out, not_175_out, not_176_out,
       not_177_out, not_178_out, not_179_out, not_180_out, not_181_out, not_182_out, not_183_out,
       not_184_out, not_185_out, not_186_out, not_187_out, not_188_out, not_189_out, not_190_out,
       not_191_out, not_192_out, not_193_out, not_194_out, not_195_out, not_196_out, not_197_out,
       not_198_out, not_199_out, not_200_out, not_201_out, not_202_out, not_203_out, not_204_out,
       not_205_out, not_206_out, not_207_out, not_208_out, not_209_out, not_210_out, not_211_out,
       not_212_out, not_213_out, not_214_out, not_215_out, not_216_out, not_217_out, not_218_out,
       not_219_out, not_220_out, not_221_out, not_222_out, not_223_out, not_224_out, not_225_out,
       not_226_out, not_227_out, not_228_out, not_229_out, not_230_out, not_231_out, not_232_out,
       not_233_out, not_234_out, not_235_out, not_236_out, not_237_out, not_238_out, not_239_out,
       not_240_out, not_241_out, not_242_out, not_243_out, not_244_out, not_245_out, not_246_out,
       not_247_out, not_248_out, not_249_out, not_250_out, not_251_out, not_252_out, not_253_out,
       not_254_out, not_255_out, not_256_out, not_257_out, not_258_out, not_259_out, not_260_out,
       not_261_out, not_262_out, not_263_out, not_264_out, not_265_out, not_266_out, not_267_out,
       not_268_out, not_269_out, not_270_out, not_271_out, not_272_out, not_273_out, not_274_out,
       not_275_out, not_276_out, not_277_out, not_278_out, not_279_out, not_280_out, not_281_out,
       not_282_out, not_283_out, not_284_out, not_285_out, not_286_out, not_287_out, not_288_out, not_289_out;

  not not_1 (not_1_out, OP5);
  not not_2 (not_2_out, OP4);
  not not_3 (not_3_out, OP3);
  not not_4 (not_4_out, OP2);
  not not_5 (not_5_out, OP1);
  not not_6 (not_6_out, OP0);
  not not_7 (not_7_out, F4);
  not not_8 (not_8_out, F3);
  not not_9 (not_9_out, F2);
  not not_10 (not_10_out, F1);
  not not_11 (not_11_out, F0);
  not not_12 (not_12_out, OP5);
  not not_13 (not_13_out, OP4);
  not not_14 (not_14_out, OP3);
  not not_15 (not_15_out, OP2);
  not not_16 (not_16_out, OP1);
  not not_17 (not_17_out, OP0);
  not not_18 (not_18_out, F4);
  not not_19 (not_19_out, F3);
  not not_20 (not_20_out, F2);
  not not_21 (not_21_out, F1);
  not not_22 (not_22_out, OP5);
  not not_23 (not_23_out, OP4);
  not not_24 (not_24_out, OP3);
  not not_25 (not_25_out, OP2);
  not not_26 (not_26_out, OP1);
  not not_27 (not_27_out, OP0);
  not not_28 (not_28_out, F4);
  not not_29 (not_29_out, F3);
  not not_30 (not_30_out, F2);
  not not_31 (not_31_out, F0);
  not not_32 (not_32_out, OP5);
  not not_33 (not_33_out, OP4);
  not not_34 (not_34_out, OP3);
  not not_35 (not_35_out, OP2);
  not not_36 (not_36_out, OP1);
  not not_37 (not_37_out, OP0);
  not not_38 (not_38_out, F4);
  not not_39 (not_39_out, F3);
  not not_40 (not_40_out, F1);
  not not_41 (not_41_out, F0);
  not not_42 (not_42_out, OP5);
  not not_43 (not_43_out, OP4);
  not not_44 (not_44_out, OP3);
  not not_45 (not_45_out, OP2);
  not not_46 (not_46_out, OP1);
  not not_47 (not_47_out, OP0);
  not not_48 (not_48_out, F4);
  not not_49 (not_49_out, F3);
  not not_50 (not_50_out, F1);
  not not_51 (not_51_out, OP5);
  not not_52 (not_52_out, OP4);
  not not_53 (not_53_out, OP3);
  not not_54 (not_54_out, OP2);
  not not_55 (not_55_out, OP1);
  not not_56 (not_56_out, OP0);
  not not_57 (not_57_out, F4);
  not not_58 (not_58_out, F3);
  not not_59 (not_59_out, OP5);
  not not_60 (not_60_out, OP4);
  not not_61 (not_61_out, OP3);
  not not_62 (not_62_out, OP2);
  not not_63 (not_63_out, OP1);
  not not_64 (not_64_out, OP0);
  not not_65 (not_65_out, F4);
  not not_66 (not_66_out, F2);
  not not_67 (not_67_out, F0);
  not not_68 (not_68_out, OP5);
  not not_69 (not_69_out, OP4);
  not not_70 (not_70_out, OP3);
  not not_71 (not_71_out, OP2);
  not not_72 (not_72_out, OP1);
  not not_73 (not_73_out, OP0);
  not not_74 (not_74_out, F4);
  not not_75 (not_75_out, F2);
  not not_76 (not_76_out, OP5);
  not not_77 (not_77_out, OP4);
  not not_78 (not_78_out, OP3);
  not not_79 (not_79_out, OP2);
  not not_80 (not_80_out, OP1);
  not not_81 (not_81_out, OP0);
  not not_82 (not_82_out, F5);
  not not_83 (not_83_out, F4);
  not not_84 (not_84_out, F2);
  not not_85 (not_85_out, F1);
  not not_86 (not_86_out, F0);
  not not_87 (not_87_out, OP5);
  not not_88 (not_88_out, OP4);
  not not_89 (not_89_out, OP3);
  not not_90 (not_90_out, OP2);
  not not_91 (not_91_out, OP1);
  not not_92 (not_92_out, OP0);
  not not_93 (not_93_out, F5);
  not not_94 (not_94_out, F4);
  not not_95 (not_95_out, F1);
  not not_96 (not_96_out, F0);
  not not_97 (not_97_out, OP5);
  not not_98 (not_98_out, OP4);
  not not_99 (not_99_out, OP3);
  not not_100 (not_100_out, OP1);
  not not_101 (not_101_out, OP0);
  not not_102 (not_102_out, OP5);
  not not_103 (not_103_out, OP4);
  not not_104 (not_104_out, OP3);
  not not_105 (not_105_out, OP1);
  not not_106 (not_106_out, OP5);
  not not_107 (not_107_out, OP4);
  not not_108 (not_108_out, OP2);
  not not_109 (not_109_out, OP1);
  not not_110 (not_110_out, OP0);
  not not_111 (not_111_out, OP5);
  not not_112 (not_112_out, OP4);
  not not_113 (not_113_out, OP1);
  not not_114 (not_114_out, OP0);
  not not_115 (not_115_out, OP5);
  not not_116 (not_116_out, OP4);
  not not_117 (not_117_out, OP2);
  not not_118 (not_118_out, OP1);
  not not_119 (not_119_out, OP5);
  not not_120 (not_120_out, OP4);
  not not_121 (not_121_out, OP2);
  not not_122 (not_122_out, OP0);
  not not_123 (not_123_out, OP5);
  not not_124 (not_124_out, OP4);
  not not_125 (not_125_out, OP1);
  not not_126 (not_126_out, OP4);
  not not_127 (not_127_out, OP3);
  not not_128 (not_128_out, OP2);
  not not_129 (not_129_out, OP4);
  not not_130 (not_130_out, OP2);
  not not_131 (not_131_out, OP5);
  not not_132 (not_132_out, OP4);
  not not_133 (not_133_out, OP3);
  not not_134 (not_134_out, OP2);
  not not_135 (not_135_out, OP1);
  not not_136 (not_136_out, OP0);
  not not_137 (not_137_out, F5);
  not not_138 (not_138_out, F4);
  not not_139 (not_139_out, F3);
  not not_140 (not_140_out, F0);
  not not_141 (not_141_out, OP5);
  not not_142 (not_142_out, OP4);
  not not_143 (not_143_out, OP0);
  not not_144 (not_144_out, OP4);
  not not_145 (not_145_out, OP3);
  not not_146 (not_146_out, OP2);
  not not_147 (not_147_out, OP1);
  not not_148 (not_148_out, OP5);
  not not_149 (not_149_out, OP4);
  not not_150 (not_150_out, OP3);
  not not_151 (not_151_out, OP5);
  not not_152 (not_152_out, OP4);
  not not_153 (not_153_out, OP3);
  not not_154 (not_154_out, OP2);
  not not_155 (not_155_out, OP1);
  not not_156 (not_156_out, OP0);
  not not_157 (not_157_out, F5);
  not not_158 (not_158_out, F4);
  not not_159 (not_159_out, F3);
  not not_160 (not_160_out, F2);
  not not_161 (not_161_out, F1);
  not not_162 (not_162_out, F0);
  not not_163 (not_163_out, OP5);
  not not_164 (not_164_out, OP4);
  not not_165 (not_165_out, OP3);
  not not_166 (not_166_out, OP2);
  not not_167 (not_167_out, OP1);
  not not_168 (not_168_out, OP0);
  not not_169 (not_169_out, F5);
  not not_170 (not_170_out, F4);
  not not_171 (not_171_out, F3);
  not not_172 (not_172_out, F2);
  not not_173 (not_173_out, OP5);
  not not_174 (not_174_out, OP4);
  not not_175 (not_175_out, OP3);
  not not_176 (not_176_out, OP2);
  not not_177 (not_177_out, OP1);
  not not_178 (not_178_out, OP0);
  not not_179 (not_179_out, F5);
  not not_180 (not_180_out, F4);
  not not_181 (not_181_out, F3);
  not not_182 (not_182_out, F2);
  not not_183 (not_183_out, F0);
  not not_184 (not_184_out, OP5);
  not not_185 (not_185_out, OP4);
  not not_186 (not_186_out, OP3);
  not not_187 (not_187_out, OP2);
  not not_188 (not_188_out, OP1);
  not not_189 (not_189_out, OP0);
  not not_190 (not_190_out, F4);
  not not_191 (not_191_out, F3);
  not not_192 (not_192_out, F2);
  not not_193 (not_193_out, F1);
  not not_194 (not_194_out, F0);
  not not_195 (not_195_out, OP5);
  not not_196 (not_196_out, OP4);
  not not_197 (not_197_out, OP3);
  not not_198 (not_198_out, OP2);
  not not_199 (not_199_out, OP1);
  not not_200 (not_200_out, OP0);
  not not_201 (not_201_out, F4);
  not not_202 (not_202_out, F3);
  not not_203 (not_203_out, F2);
  not not_204 (not_204_out, F1);
  not not_205 (not_205_out, OP5);
  not not_206 (not_206_out, OP4);
  not not_207 (not_207_out, OP3);
  not not_208 (not_208_out, OP2);
  not not_209 (not_209_out, OP1);
  not not_210 (not_210_out, OP0);
  not not_211 (not_211_out, F4);
  not not_212 (not_212_out, F3);
  not not_213 (not_213_out, F2);
  not not_214 (not_214_out, F0);
  not not_215 (not_215_out, OP5);
  not not_216 (not_216_out, OP4);
  not not_217 (not_217_out, OP3);
  not not_218 (not_218_out, OP2);
  not not_219 (not_219_out, OP1);
  not not_220 (not_220_out, OP0);
  not not_221 (not_221_out, F4);
  not not_222 (not_222_out, F3);
  not not_223 (not_223_out, F1);
  not not_224 (not_224_out, F0);
  not not_225 (not_225_out, OP5);
  not not_226 (not_226_out, OP4);
  not not_227 (not_227_out, OP3);
  not not_228 (not_228_out, OP2);
  not not_229 (not_229_out, OP1);
  not not_230 (not_230_out, OP0);
  not not_231 (not_231_out, F4);
  not not_232 (not_232_out, F3);
  not not_233 (not_233_out, F1);
  not not_234 (not_234_out, OP5);
  not not_235 (not_235_out, OP4);
  not not_236 (not_236_out, OP3);
  not not_237 (not_237_out, OP2);
  not not_238 (not_238_out, OP1);
  not not_239 (not_239_out, OP0);
  not not_240 (not_240_out, F4);
  not not_241 (not_241_out, F3);
  not not_242 (not_242_out, OP5);
  not not_243 (not_243_out, OP4);
  not not_244 (not_244_out, OP3);
  not not_245 (not_245_out, OP2);
  not not_246 (not_246_out, OP1);
  not not_247 (not_247_out, OP0);
  not not_248 (not_248_out, F4);
  not not_249 (not_249_out, F2);
  not not_250 (not_250_out, F0);
  not not_251 (not_251_out, OP5);
  not not_252 (not_252_out, OP4);
  not not_253 (not_253_out, OP3);
  not not_254 (not_254_out, OP2);
  not not_255 (not_255_out, OP1);
  not not_256 (not_256_out, OP0);
  not not_257 (not_257_out, F4);
  not not_258 (not_258_out, F2);
  not not_259 (not_259_out, OP5);
  not not_260 (not_260_out, OP4);
  not not_261 (not_261_out, OP3);
  not not_262 (not_262_out, OP2);
  not not_263 (not_263_out, OP1);
  not not_264 (not_264_out, OP0);
  not not_265 (not_265_out, F5);
  not not_266 (not_266_out, F4);
  not not_267 (not_267_out, F1);
  not not_268 (not_268_out, F0);
  not not_269 (not_269_out, OP5);
  not not_270 (not_270_out, OP4);
  not not_271 (not_271_out, OP3);
  not not_272 (not_272_out, OP1);
  not not_273 (not_273_out, OP0);
  not not_274 (not_274_out, OP5);
  not not_275 (not_275_out, OP4);
  not not_276 (not_276_out, OP3);
  not not_277 (not_277_out, OP1);
  not not_278 (not_278_out, OP4);
  not not_279 (not_279_out, OP2);
  not not_280 (not_280_out, OP5);
  not not_281 (not_281_out, OP4);
  not not_282 (not_282_out, OP3);
  not not_283 (not_283_out, OP2);
  not not_284 (not_284_out, OP1);
  not not_285 (not_285_out, OP0);
  not not_286 (not_286_out, F5);
  not not_287 (not_287_out, F4);
  not not_288 (not_288_out, F3);
  not not_289 (not_289_out, F0);
  and and_1 (and_1_out, not_1_out, not_2_out, not_3_out, not_4_out, not_5_out, not_6_out, F5, not_7_out, not_8_out, not_9_out, not_10_out, not_11_out);
  and and_2 (and_2_out, not_12_out, not_13_out, not_14_out, not_15_out, not_16_out, not_17_out, F5, not_18_out, not_19_out, not_20_out, not_21_out, F0);
  and and_3 (and_3_out, not_22_out, not_23_out, not_24_out, not_25_out, not_26_out, not_27_out, F5, not_28_out, not_29_out, not_30_out, F1, not_31_out);
  and and_4 (and_4_out, not_32_out, not_33_out, not_34_out, not_35_out, not_36_out, not_37_out, F5, not_38_out, not_39_out, F2, not_40_out, not_41_out);
  and and_5 (and_5_out, not_42_out, not_43_out, not_44_out, not_45_out, not_46_out, not_47_out, F5, not_48_out, not_49_out, F2, not_50_out, F0);
  and and_6 (and_6_out, not_51_out, not_52_out, not_53_out, not_54_out, not_55_out, not_56_out, F5, not_57_out, not_58_out, F2, F1, F0);
  and and_7 (and_7_out, not_59_out, not_60_out, not_61_out, not_62_out, not_63_out, not_64_out, F5, not_65_out, F3, not_66_out, F1, not_67_out);
  and and_8 (and_8_out, not_68_out, not_69_out, not_70_out, not_71_out, not_72_out, not_73_out, F5, not_74_out, F3, not_75_out, F1, F0);
  and and_9 (and_9_out, not_76_out, not_77_out, not_78_out, not_79_out, not_80_out, not_81_out, not_82_out, not_83_out, F3, not_84_out, not_85_out, not_86_out);
  and and_10 (and_10_out, not_87_out, not_88_out, not_89_out, not_90_out, not_91_out, not_92_out, not_93_out, not_94_out, F3, F2, not_95_out, not_96_out);
  and and_11 (and_11_out, not_97_out, not_98_out, not_99_out, OP2, not_100_out, not_101_out);
  and and_12 (and_12_out, not_102_out, not_103_out, not_104_out, OP2, not_105_out, OP0);
  and and_13 (and_13_out, not_106_out, not_107_out, OP3, not_108_out, not_109_out, not_110_out);
  and and_14 (and_14_out, not_111_out, not_112_out, OP3, OP2, not_113_out, not_114_out);
  and and_15 (and_15_out, not_115_out, not_116_out, OP3, not_117_out, not_118_out, OP0);
  and and_16 (and_16_out, not_119_out, not_120_out, OP3, not_121_out, OP1, not_122_out);
  and and_17 (and_17_out, not_123_out, not_124_out, OP3, OP2, not_125_out, OP0);
  and and_18 (and_18_out, OP5, not_126_out, not_127_out, not_128_out, OP1, OP0);
  and and_19 (and_19_out, OP5, not_129_out, OP3, not_130_out, OP1, OP0);
  and and_20 (and_20_out, not_131_out, not_132_out, not_133_out, not_134_out, not_135_out, not_136_out, not_137_out, not_138_out, not_139_out, F2, F1, not_140_out);
  and and_21 (and_21_out, not_141_out, not_142_out, OP3, OP2, OP1, not_143_out);
  and and_22 (and_22_out, OP5, not_144_out, not_145_out, not_146_out, not_147_out, OP0);
  and and_23 (and_23_out, not_148_out, not_149_out, not_150_out, OP2, OP1, OP0);
  and and_24 (and_24_out, not_151_out, not_152_out, not_153_out, not_154_out, not_155_out, not_156_out, not_157_out, not_158_out, not_159_out, not_160_out, not_161_out, not_162_out);
  and and_25 (and_25_out, not_163_out, not_164_out, not_165_out, not_166_out, not_167_out, not_168_out, not_169_out, not_170_out, not_171_out, not_172_out, F1, F0);
  and and_26 (and_26_out, not_173_out, not_174_out, not_175_out, not_176_out, not_177_out, not_178_out, not_179_out, not_180_out, not_181_out, not_182_out, F1, not_183_out);
  and and_27 (and_27_out, not_184_out, not_185_out, not_186_out, not_187_out, not_188_out, not_189_out, F5, not_190_out, not_191_out, not_192_out, not_193_out, not_194_out);
  and and_28 (and_28_out, not_195_out, not_196_out, not_197_out, not_198_out, not_199_out, not_200_out, F5, not_201_out, not_202_out, not_203_out, not_204_out, F0);
  and and_29 (and_29_out, not_205_out, not_206_out, not_207_out, not_208_out, not_209_out, not_210_out, F5, not_211_out, not_212_out, not_213_out, F1, not_214_out);
  and and_30 (and_30_out, not_215_out, not_216_out, not_217_out, not_218_out, not_219_out, not_220_out, F5, not_221_out, not_222_out, F2, not_223_out, not_224_out);
  and and_31 (and_31_out, not_225_out, not_226_out, not_227_out, not_228_out, not_229_out, not_230_out, F5, not_231_out, not_232_out, F2, not_233_out, F0);
  and and_32 (and_32_out, not_234_out, not_235_out, not_236_out, not_237_out, not_238_out, not_239_out, F5, not_240_out, not_241_out, F2, F1, F0);
  and and_33 (and_33_out, not_242_out, not_243_out, not_244_out, not_245_out, not_246_out, not_247_out, F5, not_248_out, F3, not_249_out, F1, not_250_out);
  and and_34 (and_34_out, not_251_out, not_252_out, not_253_out, not_254_out, not_255_out, not_256_out, F5, not_257_out, F3, not_258_out, F1, F0);
  and and_35 (and_35_out, not_259_out, not_260_out, not_261_out, not_262_out, not_263_out, not_264_out, not_265_out, not_266_out, F3, F2, not_267_out, not_268_out);
  and and_36 (and_36_out, not_269_out, not_270_out, not_271_out, OP2, not_272_out, not_273_out);
  and and_37 (and_37_out, not_274_out, not_275_out, not_276_out, OP2, not_277_out, OP0);
  and and_38 (and_38_out, OP5, not_278_out, OP3, not_279_out, OP1, OP0);
  and and_39 (and_39_out, not_280_out, not_281_out, not_282_out, not_283_out, not_284_out, not_285_out, not_286_out, not_287_out, not_288_out, F2, F1, not_289_out);
  or or_1 (R1_Used, and_1_out, and_2_out, and_3_out, and_4_out, and_5_out, and_6_out, and_7_out, and_8_out, and_9_out, and_10_out, and_11_out, and_12_out, and_13_out, and_14_out, and_15_out, and_16_out, and_17_out, and_18_out, and_19_out, and_20_out, and_21_out, and_22_out, and_23_out);
  or or_2 (R2_Used, and_24_out, and_25_out, and_26_out, and_27_out, and_28_out, and_29_out, and_30_out, and_31_out, and_32_out, and_33_out, and_34_out, and_35_out, and_36_out, and_37_out, and_38_out, and_39_out);
endmodule

module \load_use检测  (
  input  [5:0] OP,
  input  [4:0] EX_WriteReg_num,
  input  EX_RegWrite,
  input  EX_load,
  input  [4:0] MEM_WriteReg_num,
  input  MEM_RegWrite,
  input  [5:0] Func,
  input  mem_load,
  input  [4:0] ID_R1_num,
  input  [4:0] ID_R2_num,
  output load_use,
  output [1:0] sel_a,
  output [1:0] sel_b
);

  wire and_1_out, and_2_out, and_3_out, and_4_out, and_5_out, and_6_out, and_7_out, and_8_out, and_9_out,
       and_10_out, and_11_out, and_12_out, and_13_out, and_14_out, and_15_out, and_16_out, and_17_out,
       and_18_out, comparator_1_eq, comparator_2_eq, comparator_3_eq, comparator_4_eq, comparator_5_eq,
       comparator_6_eq, nor_1_out, nor_2_out, not_1_out, not_2_out, or_1_out, or_2_out, or_3_out, or_4_out,
       \源寄存器使用情况_1_r1_used , \源寄存器使用情况_1_r2_used ;

  \源寄存器使用情况  \u_源寄存器使用情况_1  (
    .OP0(OP[0]), .OP1(OP[1]), .OP2(OP[2]), .OP3(OP[3]), .OP4(OP[4]), .OP5(OP[5]), .F0(Func[0]), .F1(Func[1]),
    .F2(Func[2]), .F3(Func[3]), .F4(Func[4]), .F5(Func[5]), .R1_Used(\源寄存器使用情况_1_r1_used ),
    .R2_Used(\源寄存器使用情况_1_r2_used ));
  or or_1 (or_1_out, ID_R2_num[0], ID_R2_num[1], ID_R2_num[2], ID_R2_num[3], ID_R2_num[4]);
  or or_2 (or_2_out, ID_R1_num[0], ID_R1_num[1], ID_R1_num[2], ID_R1_num[3], ID_R1_num[4]);
  Comparator #(.width(5), .mode("unsigned")) comparator_1 (
    .a(ID_R2_num), .b(MEM_WriteReg_num), .eq(comparator_1_eq));  // open: gt, lt
  or or_3 (or_3_out, ID_R1_num[0], ID_R1_num[1], ID_R1_num[2], ID_R1_num[3], ID_R1_num[4]);
  Comparator #(.width(5), .mode("unsigned")) comparator_2 (
    .a(ID_R1_num), .b(EX_WriteReg_num), .eq(comparator_2_eq));  // open: gt, lt
  and and_1 (and_1_out, comparator_2_eq, EX_load);
  or or_4 (or_4_out, ID_R2_num[0], ID_R2_num[1], ID_R2_num[2], ID_R2_num[3], ID_R2_num[4]);
  Comparator #(.width(5), .mode("unsigned")) comparator_3 (
    .a(ID_R2_num), .b(EX_WriteReg_num), .eq(comparator_3_eq));  // open: gt, lt
  and and_2 (and_2_out, comparator_3_eq, EX_load);
  Comparator #(.width(5), .mode("unsigned")) comparator_4 (
    .a(ID_R1_num), .b(EX_WriteReg_num), .eq(comparator_4_eq));  // open: gt, lt
  Comparator #(.width(5), .mode("unsigned")) comparator_5 (
    .a(ID_R1_num), .b(MEM_WriteReg_num), .eq(comparator_5_eq));  // open: gt, lt
  and and_3 (and_3_out, or_1_out, \源寄存器使用情况_1_r2_used );
  Comparator #(.width(5), .mode("unsigned")) comparator_6 (
    .a(ID_R2_num), .b(EX_WriteReg_num), .eq(comparator_6_eq));  // open: gt, lt
  and and_4 (and_4_out, ~EX_load, comparator_6_eq, EX_RegWrite);  // AND_Gate
  and and_5 (and_5_out, comparator_1_eq, MEM_RegWrite);
  and and_6 (and_6_out, or_2_out, \源寄存器使用情况_1_r1_used );
  and and_7 (and_7_out, ~EX_load, comparator_4_eq, EX_RegWrite);  // AND_Gate
  and and_8 (and_8_out, comparator_5_eq, MEM_RegWrite);
  and and_9 (and_9_out, and_3_out, and_4_out);
  and and_10 (and_10_out, and_3_out, and_5_out);
  not not_1 (not_1_out, mem_load);
  and and_11 (and_11_out, or_3_out, \源寄存器使用情况_1_r1_used , and_1_out);
  and and_12 (and_12_out, or_4_out, \源寄存器使用情况_1_r2_used , and_2_out);
  assign sel_a = and_13_out ? 2'b01 : 2'bz;  // Controlled_Buffer controlled_buffer_1
  and and_13 (and_13_out, and_6_out, and_7_out);
  and and_14 (and_14_out, and_6_out, and_8_out);
  not not_2 (not_2_out, mem_load);
  assign sel_b = and_9_out ? 2'b01 : 2'bz;  // Controlled_Buffer controlled_buffer_2
  and and_15 (and_15_out, and_10_out, ~and_9_out, mem_load);  // AND_Gate
  and and_16 (and_16_out, and_10_out, ~and_9_out, not_1_out);  // AND_Gate
  or or_5 (load_use, and_11_out, and_12_out);
  assign sel_a = and_17_out ? 2'b11 : 2'bz;  // Controlled_Buffer controlled_buffer_3
  and and_17 (and_17_out, and_14_out, ~and_13_out, mem_load);  // AND_Gate
  assign sel_a = and_18_out ? 2'b10 : 2'bz;  // Controlled_Buffer controlled_buffer_4
  and and_18 (and_18_out, and_14_out, not_2_out, ~and_13_out);  // AND_Gate
  assign sel_b = and_15_out ? 2'b11 : 2'bz;  // Controlled_Buffer controlled_buffer_5
  assign sel_b = and_16_out ? 2'b10 : 2'bz;  // Controlled_Buffer controlled_buffer_6
  assign sel_a = nor_1_out ? 2'b00 : 2'bz;  // Controlled_Buffer controlled_buffer_7
  nor nor_1 (nor_1_out, and_13_out, and_17_out, and_18_out);
  assign sel_b = nor_2_out ? 2'b00 : 2'bz;  // Controlled_Buffer controlled_buffer_8
  nor nor_2 (nor_2_out, and_9_out, and_15_out, and_16_out);

  // Other names for the same wires on the sheet: OP_CODE[5:0] = OP
endmodule

module IF_ID (
  input  [31:0] IR,
  input  [31:0] PC,
  input  miss,
  input  prejump,
  input  [7:0] hit_num,
  input  CLK,
  input  \同步清零_气泡_高电平有效 ,
  input  \使能端_低电平正常工作 ,
  output [31:0] IR_2,
  output [31:0] PC_2,
  output miss_2,
  output prejump_2,
  output [7:0] hitnum
);

  wire multiplexer_2_out, multiplexer_3_out, not_1_out;
  wire [7:0] multiplexer_4_out;
  wire [31:0] multiplexer_1_out, multiplexer_5_out;

  Multiplexer #(.width(32), .enable("false")) multiplexer_1 (
    .in0(PC), .in1({32{1'b0}}), .out(multiplexer_1_out), .sel(\同步清零_气泡_高电平有效 ));
  Multiplexer #(.enable("false")) multiplexer_2 (
    .in0(miss), .in1(1'b0), .out(multiplexer_2_out), .sel(\同步清零_气泡_高电平有效 ));
  Multiplexer #(.enable("false")) multiplexer_3 (
    .in0(prejump), .in1(1'b0), .out(multiplexer_3_out), .sel(\同步清零_气泡_高电平有效 ));
  Multiplexer #(.width(8), .enable("false")) multiplexer_4 (
    .in0(hit_num), .in1({8{1'b0}}), .out(multiplexer_4_out), .sel(\同步清零_气泡_高电平有效 ));
  Multiplexer #(.width(32), .enable("false")) multiplexer_5 (
    .in0(IR), .in1({32{1'b0}}), .out(multiplexer_5_out), .sel(\同步清零_气泡_高电平有效 ));
  not not_1 (not_1_out, \使能端_低电平正常工作 );
  Register #(.width(32)) register_1 (.D(multiplexer_5_out), .en(not_1_out), .Q(IR_2), .clk(CLK));  // open: clr
  Register #(.width(32)) register_2 (.D(multiplexer_1_out), .en(not_1_out), .Q(PC_2), .clk(CLK));  // open: clr
  Register #(.width(1)) register_3 (.D(multiplexer_2_out), .en(not_1_out), .Q(miss_2), .clk(CLK));  // open: clr
  Register #(.width(1)) register_4 (.D(multiplexer_3_out), .en(not_1_out), .Q(prejump_2), .clk(CLK));  // open: clr
  Register register_5 (.D(multiplexer_4_out), .en(not_1_out), .Q(hitnum), .clk(CLK));  // open: clr
endmodule

module ID_EX (
  input  CLK,
  input  MemtoReg,
  input  RegWrite,
  input  jal,
  input  [4:0] W_num,
  input  JMP,
  input  JR,
  input  MemWrite,
  input  Syscall,
  input  [3:0] ALUOP,
  input  AluSrcB,
  input  SignExt,
  input  [31:0] IR,
  input  [31:0] PC,
  input  [31:0] A,
  input  [31:0] B,
  input  beq,
  input  bne,
  input  bgtz,
  input  lh,
  input  srlv,
  input  [1:0] sel_a,
  input  [1:0] sel_b,
  input  miss,
  input  prejump,
  input  [7:0] hit_num,
  input  \同步清零_气泡_高电平有效 ,
  input  \使能端_低电平正常工作 ,
  output MemToReg_2,
  output RegWrite_2,
  output jal_2,
  output [4:0] W_num_2,
  output JMP_2,
  output JR_2,
  output MemWrite_2,
  output Syscall_2,
  output [3:0] ALUOP_2,
  output AluSrcB_2,
  output SignExt_2,
  output [31:0] IR_2,
  output [31:0] PC_2,
  output [31:0] A_2,
  output [31:0] B_2,
  output beq_2,
  output bne_2,
  output bgtz_2,
  output lh_2,
  output srlv_2,
  output [1:0] sel_a_2,
  output [1:0] sel_b_2,
  output miss_2,
  output prejump_2,
  output [7:0] hit_num_2
);

  wire multiplexer_1_out, multiplexer_2_out, multiplexer_3_out, multiplexer_5_out, multiplexer_6_out,
       multiplexer_7_out, multiplexer_8_out, multiplexer_10_out, multiplexer_11_out, multiplexer_16_out,
       multiplexer_17_out, multiplexer_18_out, multiplexer_19_out, multiplexer_20_out, multiplexer_23_out,
       multiplexer_24_out, not_1_out, undriven, undriven_2, undriven_3, undriven_4, undriven_5, undriven_6,
       undriven_7, undriven_8, undriven_9;
  wire [1:0] multiplexer_21_out, multiplexer_22_out;
  wire [3:0] multiplexer_9_out;
  wire [4:0] multiplexer_4_out;
  wire [7:0] multiplexer_25_out;
  wire [31:0] multiplexer_12_out, multiplexer_13_out, multiplexer_14_out, multiplexer_15_out;

  Multiplexer #(.enable("false")) multiplexer_1 (
    .in0(MemtoReg), .in1(1'b0), .out(multiplexer_1_out), .sel(\同步清零_气泡_高电平有效 ));
  Multiplexer #(.enable("false")) multiplexer_2 (
    .in0(RegWrite), .in1(1'b0), .out(multiplexer_2_out), .sel(\同步清零_气泡_高电平有效 ));
  Multiplexer #(.enable("false")) multiplexer_3 (.in0(jal), .in1(1'b0), .out(multiplexer_3_out), .sel(\同步清零_气泡_高电平有效 ));
  Multiplexer #(.width(5), .enable("false")) multiplexer_4 (
    .in0(W_num), .in1({5{1'b0}}), .out(multiplexer_4_out), .sel(\同步清零_气泡_高电平有效 ));
  Multiplexer #(.enable("false")) multiplexer_5 (.in0(JMP), .in1(1'b0), .out(multiplexer_5_out), .sel(\同步清零_气泡_高电平有效 ));
  Multiplexer #(.enable("false")) multiplexer_6 (.in0(JR), .in1(1'b0), .out(multiplexer_6_out), .sel(\同步清零_气泡_高电平有效 ));
  Multiplexer #(.enable("false")) multiplexer_7 (
    .in0(MemWrite), .in1(1'b0), .out(multiplexer_7_out), .sel(\同步清零_气泡_高电平有效 ));
  Multiplexer #(.enable("false")) multiplexer_8 (
    .in0(Syscall), .in1(1'b0), .out(multiplexer_8_out), .sel(\同步清零_气泡_高电平有效 ));
  Multiplexer #(.width(4), .enable("false")) multiplexer_9 (
    .in0(ALUOP), .in1(4'b0000), .out(multiplexer_9_out), .sel(\同步清零_气泡_高电平有效 ));
  Multiplexer #(.enable("false")) multiplexer_10 (
    .in0(AluSrcB), .in1(1'b0), .out(multiplexer_10_out), .sel(\同步清零_气泡_高电平有效 ));
  Multiplexer #(.enable("false")) multiplexer_11 (
    .in0(SignExt), .in1(1'b0), .out(multiplexer_11_out), .sel(\同步清零_气泡_高电平有效 ));
  Multiplexer #(.width(32), .enable("false")) multiplexer_12 (
    .in0(IR), .in1({32{1'b0}}), .out(multiplexer_12_out), .sel(\同步清零_气泡_高电平有效 ));
  Multiplexer #(.width(32), .enable("false")) multiplexer_13 (
    .in0(PC), .in1({32{1'b0}}), .out(multiplexer_13_out), .sel(\同步清零_气泡_高电平有效 ));
  Multiplexer #(.width(32), .enable("false")) multiplexer_14 (
    .in0(A), .in1({32{1'b0}}), .out(multiplexer_14_out), .sel(\同步清零_气泡_高电平有效 ));
  Multiplexer #(.width(32), .enable("false")) multiplexer_15 (
    .in0(B), .in1({32{1'b0}}), .out(multiplexer_15_out), .sel(\同步清零_气泡_高电平有效 ));
  Multiplexer #(.enable("false")) multiplexer_16 (
    .in0(beq), .in1(1'b0), .out(multiplexer_16_out), .sel(\同步清零_气泡_高电平有效 ));
  Multiplexer #(.enable("false")) multiplexer_17 (
    .in0(bne), .in1(1'b0), .out(multiplexer_17_out), .sel(\同步清零_气泡_高电平有效 ));
  Multiplexer #(.enable("false")) multiplexer_18 (
    .in0(bgtz), .in1(1'b0), .out(multiplexer_18_out), .sel(\同步清零_气泡_高电平有效 ));
  Multiplexer #(.enable("false")) multiplexer_19 (
    .in0(lh), .in1(1'b0), .out(multiplexer_19_out), .sel(\同步清零_气泡_高电平有效 ));
  Multiplexer #(.enable("false")) multiplexer_20 (
    .in0(srlv), .in1(1'b0), .out(multiplexer_20_out), .sel(\同步清零_气泡_高电平有效 ));
  Multiplexer #(.width(2), .enable("false")) multiplexer_21 (
    .in0(sel_a), .in1(2'b00), .out(multiplexer_21_out), .sel(\同步清零_气泡_高电平有效 ));
  Multiplexer #(.width(2), .enable("false")) multiplexer_22 (
    .in0(sel_b), .in1(2'b00), .out(multiplexer_22_out), .sel(\同步清零_气泡_高电平有效 ));
  Multiplexer #(.enable("false")) multiplexer_23 (
    .in0(miss), .in1(1'b0), .out(multiplexer_23_out), .sel(\同步清零_气泡_高电平有效 ));
  Multiplexer #(.enable("false")) multiplexer_24 (
    .in0(prejump), .in1(1'b0), .out(multiplexer_24_out), .sel(\同步清零_气泡_高电平有效 ));
  Multiplexer #(.width(8), .enable("false")) multiplexer_25 (
    .in0(hit_num), .in1({8{1'b0}}), .out(multiplexer_25_out), .sel(\同步清零_气泡_高电平有效 ));
  Register #(.width(1)) register_1 (.D(multiplexer_1_out), .en(not_1_out), .Q(MemToReg_2), .clk(CLK));  // open: clr
  Register #(.width(1)) register_2 (.D(multiplexer_2_out), .en(not_1_out), .Q(RegWrite_2), .clk(CLK));  // open: clr
  Register #(.width(1)) register_3 (.D(multiplexer_3_out), .en(not_1_out), .Q(jal_2), .clk(CLK));  // open: clr
  Register #(.width(5)) register_4 (.D(multiplexer_4_out), .en(not_1_out), .Q(W_num_2), .clk(CLK));  // open: clr
  Register #(.width(1)) register_5 (.D(multiplexer_5_out), .en(not_1_out), .Q(JMP_2), .clk(CLK));  // open: clr
  Register #(.width(1)) register_6 (.D(multiplexer_6_out), .en(not_1_out), .Q(JR_2), .clk(CLK));  // open: clr
  Register #(.width(1)) register_7 (.D(multiplexer_7_out), .en(not_1_out), .Q(MemWrite_2), .clk(CLK));  // open: clr
  Register #(.width(1)) register_8 (.D(multiplexer_8_out), .en(not_1_out), .Q(Syscall_2), .clk(CLK));  // open: clr
  Register #(.width(4)) register_9 (.D(multiplexer_9_out), .en(not_1_out), .Q(ALUOP_2), .clk(CLK));  // open: clr
  Register #(.width(1)) register_10 (.D(multiplexer_10_out), .en(not_1_out), .Q(AluSrcB_2), .clk(CLK));  // open: clr
  Register #(.width(1)) register_11 (.D(multiplexer_11_out), .en(not_1_out), .Q(SignExt_2), .clk(CLK));  // open: clr
  Register #(.width(32)) register_12 (.D(multiplexer_12_out), .en(not_1_out), .Q(IR_2), .clk(CLK));  // open: clr
  Register #(.width(32)) register_13 (.D(multiplexer_13_out), .en(not_1_out), .Q(PC_2), .clk(CLK));  // open: clr
  Register #(.width(32)) register_14 (.D(multiplexer_14_out), .en(not_1_out), .Q(A_2), .clk(CLK));  // open: clr
  Register #(.width(32)) register_15 (.D(multiplexer_15_out), .en(not_1_out), .Q(B_2), .clk(CLK));  // open: clr
  Register #(.width(1)) register_16 (.D(multiplexer_16_out), .en(not_1_out), .Q(beq_2), .clk(CLK));  // open: clr
  Register #(.width(1)) register_17 (.D(multiplexer_17_out), .en(not_1_out), .Q(bne_2), .clk(CLK), .clr(undriven));
  Register #(.width(1)) register_18 (.D(multiplexer_18_out), .en(not_1_out), .Q(bgtz_2), .clk(CLK), .clr(undriven_2));
  Register #(.width(1)) register_19 (.D(multiplexer_19_out), .en(not_1_out), .Q(lh_2), .clk(CLK), .clr(undriven_3));
  Register #(.width(1)) register_20 (.D(multiplexer_20_out), .en(not_1_out), .Q(srlv_2), .clk(CLK), .clr(undriven_4));
  Register #(.width(2)) register_21 (.D(multiplexer_21_out), .en(not_1_out), .Q(sel_a_2), .clk(CLK), .clr(undriven_5));
  Register #(.width(2)) register_22 (.D(multiplexer_22_out), .en(not_1_out), .Q(sel_b_2), .clk(CLK), .clr(undriven_6));
  Register #(.width(1)) register_23 (.D(multiplexer_23_out), .en(not_1_out), .Q(miss_2), .clk(CLK), .clr(undriven_7));
  Register #(.width(1)) register_24 (
    .D(multiplexer_24_out), .en(not_1_out), .Q(prejump_2), .clk(CLK), .clr(undriven_8));
  Register register_25 (.D(multiplexer_25_out), .en(not_1_out), .Q(hit_num_2), .clk(CLK), .clr(undriven_9));
  not not_1 (not_1_out, \使能端_低电平正常工作 );
endmodule

module EX_MEM (
  input  CLK,
  input  MemtoReg,
  input  RegWrite,
  input  jal,
  input  [4:0] W_num,
  input  lh,
  input  MemWrite,
  input  pause,
  input  [31:0] IR,
  input  [31:0] PC,
  input  [31:0] ALU_Result,
  input  [31:0] B,
  input  \同步清零_气泡_高电平有效 ,
  input  \使能端_低电平正常工作 ,
  output MemToReg_2,
  output RegWrite_2,
  output jal_2,
  output [4:0] W_num_2,
  output lh_2,
  output MemWrite_2,
  output pause_2,
  output [31:0] IR_2,
  output [31:0] PC_2,
  output [31:0] ALU_Result_2,
  output [31:0] B_2
);

  wire multiplexer_1_out, multiplexer_2_out, multiplexer_3_out, multiplexer_5_out, multiplexer_6_out,
       multiplexer_7_out, not_1_out;
  wire [4:0] multiplexer_4_out;
  wire [31:0] multiplexer_8_out, multiplexer_9_out, multiplexer_10_out, multiplexer_11_out;

  Multiplexer #(.enable("false")) multiplexer_1 (
    .in0(MemtoReg), .in1(1'b0), .out(multiplexer_1_out), .sel(\同步清零_气泡_高电平有效 ));
  Multiplexer #(.enable("false")) multiplexer_2 (
    .in0(RegWrite), .in1(1'b0), .out(multiplexer_2_out), .sel(\同步清零_气泡_高电平有效 ));
  Multiplexer #(.enable("false")) multiplexer_3 (.in0(jal), .in1(1'b0), .out(multiplexer_3_out), .sel(\同步清零_气泡_高电平有效 ));
  Multiplexer #(.width(5), .enable("false")) multiplexer_4 (
    .in0(W_num), .in1({5{1'b0}}), .out(multiplexer_4_out), .sel(\同步清零_气泡_高电平有效 ));
  Multiplexer #(.enable("false")) multiplexer_5 (.in0(lh), .in1(1'b0), .out(multiplexer_5_out), .sel(\同步清零_气泡_高电平有效 ));
  Multiplexer #(.enable("false")) multiplexer_6 (
    .in0(MemWrite), .in1(1'b0), .out(multiplexer_6_out), .sel(\同步清零_气泡_高电平有效 ));
  Multiplexer #(.enable("false")) multiplexer_7 (
    .in0(pause), .in1(1'b0), .out(multiplexer_7_out), .sel(\同步清零_气泡_高电平有效 ));
  Multiplexer #(.width(32), .enable("false")) multiplexer_8 (
    .in0(IR), .in1({32{1'b0}}), .out(multiplexer_8_out), .sel(\同步清零_气泡_高电平有效 ));
  Multiplexer #(.width(32), .enable("false")) multiplexer_9 (
    .in0(PC), .in1({32{1'b0}}), .out(multiplexer_9_out), .sel(\同步清零_气泡_高电平有效 ));
  Multiplexer #(.width(32), .enable("false")) multiplexer_10 (
    .in0(ALU_Result), .in1({32{1'b0}}), .out(multiplexer_10_out), .sel(\同步清零_气泡_高电平有效 ));
  Multiplexer #(.width(32), .enable("false")) multiplexer_11 (
    .in0(B), .in1({32{1'b0}}), .out(multiplexer_11_out), .sel(\同步清零_气泡_高电平有效 ));
  Register #(.width(1)) register_1 (.D(multiplexer_1_out), .en(not_1_out), .Q(MemToReg_2), .clk(CLK), .clr(1'b0));
  Register #(.width(1)) register_2 (.D(multiplexer_2_out), .en(not_1_out), .Q(RegWrite_2), .clk(CLK), .clr(1'b0));
  Register #(.width(1)) register_3 (.D(multiplexer_3_out), .en(not_1_out), .Q(jal_2), .clk(CLK), .clr(1'b0));
  Register #(.width(5)) register_4 (.D(multiplexer_4_out), .en(not_1_out), .Q(W_num_2), .clk(CLK), .clr(1'b0));
  Register #(.width(1)) register_5 (.D(multiplexer_5_out), .en(not_1_out), .Q(lh_2), .clk(CLK), .clr(1'b0));
  Register #(.width(1)) register_6 (.D(multiplexer_6_out), .en(not_1_out), .Q(MemWrite_2), .clk(CLK), .clr(1'b0));
  Register #(.width(1)) register_7 (.D(multiplexer_7_out), .en(not_1_out), .Q(pause_2), .clk(CLK), .clr(1'b0));
  Register #(.width(32)) register_8 (.D(multiplexer_8_out), .en(not_1_out), .Q(IR_2), .clk(CLK), .clr(1'b0));
  Register #(.width(32)) register_9 (.D(multiplexer_9_out), .en(not_1_out), .Q(PC_2), .clk(CLK), .clr(1'b0));
  Register #(.width(32)) register_10 (.D(multiplexer_10_out), .en(not_1_out), .Q(ALU_Result_2), .clk(CLK), .clr(1'b0));
  Register #(.width(32)) register_11 (.D(multiplexer_11_out), .en(not_1_out), .Q(B_2), .clk(CLK), .clr(1'b0));
  not not_1 (not_1_out, \使能端_低电平正常工作 );
endmodule

module MEM_WB (
  input  CLK,
  input  MemtoReg,
  input  RegWrite,
  input  jal,
  input  [4:0] W_num,
  input  pause,
  input  [31:0] IR,
  input  [31:0] PC,
  input  [31:0] ALU_Result,
  input  [31:0] Dout,
  input  \同步清零_气泡_高电平有效 ,
  input  \使能端_低电平正常工作 ,
  output MemToReg_2,
  output RegWrite_2,
  output jal_2,
  output [4:0] W_num_2,
  output pause_2,
  output [31:0] IR_2,
  output [31:0] PC_2,
  output [31:0] ALU_Result_2,
  output [31:0] Dout_2
);

  wire multiplexer_1_out, multiplexer_2_out, multiplexer_3_out, multiplexer_5_out, not_1_out;
  wire [4:0] multiplexer_4_out;
  wire [31:0] multiplexer_6_out, multiplexer_7_out, multiplexer_8_out, multiplexer_9_out;

  Multiplexer #(.enable("false")) multiplexer_1 (
    .in0(MemtoReg), .in1(1'b0), .out(multiplexer_1_out), .sel(\同步清零_气泡_高电平有效 ));
  Multiplexer #(.enable("false")) multiplexer_2 (
    .in0(RegWrite), .in1(1'b0), .out(multiplexer_2_out), .sel(\同步清零_气泡_高电平有效 ));
  Multiplexer #(.enable("false")) multiplexer_3 (.in0(jal), .in1(1'b0), .out(multiplexer_3_out), .sel(\同步清零_气泡_高电平有效 ));
  Multiplexer #(.width(5), .enable("false")) multiplexer_4 (
    .in0(W_num), .in1({5{1'b0}}), .out(multiplexer_4_out), .sel(\同步清零_气泡_高电平有效 ));
  Multiplexer #(.enable("false")) multiplexer_5 (
    .in0(pause), .in1(1'b0), .out(multiplexer_5_out), .sel(\同步清零_气泡_高电平有效 ));
  Multiplexer #(.width(32), .enable("false")) multiplexer_6 (
    .in0(IR), .in1({32{1'b0}}), .out(multiplexer_6_out), .sel(\同步清零_气泡_高电平有效 ));
  Multiplexer #(.width(32), .enable("false")) multiplexer_7 (
    .in0(PC), .in1({32{1'b0}}), .out(multiplexer_7_out), .sel(\同步清零_气泡_高电平有效 ));
  Multiplexer #(.width(32), .enable("false")) multiplexer_8 (
    .in0(ALU_Result), .in1({32{1'b0}}), .out(multiplexer_8_out), .sel(\同步清零_气泡_高电平有效 ));
  Multiplexer #(.width(32), .enable("false")) multiplexer_9 (
    .in0(Dout), .in1({32{1'b0}}), .out(multiplexer_9_out), .sel(\同步清零_气泡_高电平有效 ));
  Register #(.width(1)) register_1 (.D(multiplexer_1_out), .en(not_1_out), .Q(MemToReg_2), .clk(CLK), .clr(1'b0));
  Register #(.width(1)) register_2 (.D(multiplexer_2_out), .en(not_1_out), .Q(RegWrite_2), .clk(CLK), .clr(1'b0));
  Register #(.width(1)) register_3 (.D(multiplexer_3_out), .en(not_1_out), .Q(jal_2), .clk(CLK), .clr(1'b0));
  Register #(.width(5)) register_4 (.D(multiplexer_4_out), .en(not_1_out), .Q(W_num_2), .clk(CLK), .clr(1'b0));
  Register #(.width(1)) register_5 (.D(multiplexer_5_out), .en(not_1_out), .Q(pause_2), .clk(CLK), .clr(1'b0));
  Register #(.width(32)) register_6 (.D(multiplexer_6_out), .en(not_1_out), .Q(IR_2), .clk(CLK), .clr(1'b0));
  Register #(.width(32)) register_7 (.D(multiplexer_7_out), .en(not_1_out), .Q(PC_2), .clk(CLK), .clr(1'b0));
  Register #(.width(32)) register_8 (.D(multiplexer_8_out), .en(not_1_out), .Q(ALU_Result_2), .clk(CLK), .clr(1'b0));
  Register #(.width(32)) register_9 (.D(multiplexer_9_out), .en(not_1_out), .Q(Dout_2), .clk(CLK), .clr(1'b0));
  not not_1 (not_1_out, \使能端_低电平正常工作 );
endmodule

module \重定向流水线_动态分支预测  (
);

  wire AluSrcB, and_1_out, and_2_out, and_3_out, and_5_out, and_9_out, and_10_out, and_11_out, and_12_out,
       and_13_out, and_14_out, and_15_out, and_16_out, and_17_out, BGTZ, bgtz_ex, bht_load, bht_update,
       branch, bubble_1, bubble_2, CLK, comparator_1_eq, en, en_pc, ex_cj, ex_load, ex_mem_1_jal_2,
       ex_mem_1_memtoreg_2, ex_mem_1_memwrite_2, ex_mem_1_pause_2, ex_miss, ex_prejump, ex_regwrite, Go,
       id_ex_1_beq_2, id_ex_1_bne_2, id_ex_1_jal_2, id_ex_1_lh_2, id_ex_1_memtoreg_2, id_ex_1_memwrite_2,
       id_jal, id_miss, id_prejump, id_regdst, if_miss, if_prejump, IR1, IR2, IR3, jal, JMP, JR, LH, LH_MEM,
       load_use, mem_load, mem_regwrite, mem_wb_1_memtoreg_2, nor_1_out, nor_2_out, not_1_out, not_2_out,
       not_3_out, not_4_out, not_5_out, not_6_out, not_7_out, or_2_out, or_3_out, or_5_out, or_12_out, pause,
       pre_bubble, registerfile_1_p9, RST, sel, SignedExt, SRLV, still_j, succeed, syscall, syscall_ex, W1,
       W2, W3, wb_pause, WB_RegWrite, \硬布线控制器_1_alu_src , \硬布线控制器_1_beq , \硬布线控制器_1_bne , \硬布线控制器_1_jmp ,
       \硬布线控制器_1_jr , \硬布线控制器_1_memtoreg , \硬布线控制器_1_memwrite , \硬布线控制器_1_regwrite , \硬布线控制器_1_signedext ;
  wire [1:0] initial_state, multiplexer_6_out, sel_a, sel_a_id, sel_b, sel_b_id;
  wire [3:0] id_ex_1_aluop_2, \硬布线控制器_1_alu_op ;
  wire [4:0] ex_w_num, id_r1_num, id_r2_num, id_w_num, mem_w_num, multiplexer_5_out, W_num;
  wire [5:0] Func, OP;
  wire [7:0] ex_hitnum, id_hitnum, if_hitnum;
  wire [15:0] imme, \LoadUse次数 , wb_imme, \总周期数 , \插入气泡数 , \无条件分支数 , \条件分支成功数 ;
  wire [25:6] if_id_1_ir_2;
  wire [25:16] instr_index;
  wire [31:0] adder_1_out, adder_2_out, adder_3_out, adder_4_out, adder_5_out, adder_6_out, B,
       bit_extender_1_out, bit_extender_2_out, bit_extender_3_out, bit_extender_4_out, bit_extender_5_out,
       controlled_buffer_16_out, ex_mem_1_b_2, ex_mem_1_ir_2, EX_PC, ID_PC, IF_PC, jumpaddr, LedData,
       MEM_alu, MEM_PC, mips_alu_1_result, mips_ram_1_p8, multi_A, multiplexer_7_out, multiplexer_8_out,
       multiplexer_10_out, no_pre_PC, PC, R1, R2, Reg_din, registerfile_1_p7, registerfile_1_p8, rom_1_data,
       show_data, wb_alu, wb_dout, WB_PC;
  wire [31:16] mem_wb_1_ir_2;
  wire [31:26] id_ex_1_ir_2;

  Button \u_总复位  (.out(RST));
  Button _1 (.out(IR1));
  Button _2 (.out(IR2));
  Button _3 (.out(IR3));
  Button \u_继续运行  (.out(Go));
  LED led_1 (.in(W1));
  LED led_2 (.in(W2));
  LED led_3 (.in(W3));
  Register #(.width(32)) u_PC (.D(PC), .en(en_pc), .Q(IF_PC), .clk(CLK), .clr(RST));
  Hex_Digit_Display hex_digit_display_1 (.value(LedData[31:28]));  // open: dp
  BHT bht_1 (
    .BlockDataIn(no_pre_PC), .Addr(IF_PC), .BlkDataReady(bht_load), .CLK(CLK), .stateReady(bht_update),
    .succeed(succeed), .initial_state(initial_state), .Miss(if_miss), .DataOut(jumpaddr),
    .pre_jump(if_prejump), .hit_num(if_hitnum), .update_num(ex_hitnum), .load_pc(EX_PC), .ex_Miss(ex_miss));
  and and_1 (and_1_out, en, JMP);
  and and_2 (and_2_out, en, branch);
  and and_3 (and_3_out, en, load_use);
  and and_4 (en_pc, en, ~load_use);  // AND_Gate
  Hex_Digit_Display hex_digit_display_2 (.value(LedData[27:24]));  // open: dp
  Hex_Digit_Display hex_digit_display_3 (.value(LedData[23:20]));  // open: dp
  not not_1 (not_1_out, en_pc);
  Counter #(.width(16), .max('hffff)) counter_1 (
    .count(and_1_out), .Q(\无条件分支数 ), .clk(CLK), .clr(RST));  // open: load, D, carry
  Counter #(.width(16), .max('hffff)) counter_2 (.count(en), .Q(\总周期数 ), .clk(CLK), .clr(RST));  // open: load, D, carry
  Counter #(.width(16), .max('hffff)) counter_3 (
    .count(and_2_out), .Q(\条件分支成功数 ), .clk(CLK), .clr(RST));  // open: load, D, carry
  Counter #(.width(16), .max('hffff)) counter_4 (
    .count(and_3_out), .Q(\LoadUse次数 ), .clk(CLK), .clr(RST));  // open: load, D, carry
  or or_1 (en, Go, ~wb_pause);  // OR_Gate
  Hex_Digit_Display hex_digit_display_4 (.value(LedData[19:16]));  // open: dp
  Hex_Digit_Display hex_digit_display_5 (.value(LedData[15:12]));  // open: dp
  or or_2 (or_2_out, bubble_1, RST);
  IF_ID if_id_1 (
    .IR(rom_1_data), .PC(IF_PC), .IR_2({OP, if_id_1_ir_2, Func}), .PC_2(ID_PC), .CLK(CLK),
    .\使能端_低电平正常工作 (not_1_out), .\同步清零_气泡_高电平有效 (or_2_out), .miss(if_miss), .miss_2(id_miss),
    .prejump(if_prejump), .prejump_2(id_prejump), .hit_num(if_hitnum), .hitnum(id_hitnum));
  ROM #(.addrWidth(10), .dataWidth(32)) rom_1 (.addr(IF_PC[11:2]), .data(rom_1_data));  // open: sel
  and and_5 (and_5_out, sel, syscall_ex);
  Hex_Digit_Display hex_digit_display_6 (.value(LedData[7:4]));  // open: dp
  Hex_Digit_Display hex_digit_display_7 (.value(LedData[11:8]));  // open: dp
  Clock clock_1 (.out(CLK));
  or or_3 (or_3_out, bubble_2, RST);
  Register #(.width(32)) register_1 (.D(show_data), .en(and_5_out), .Q(LedData), .clk(CLK));  // open: clr
  and and_6 (pause, ~sel, syscall_ex);  // AND_Gate
  Hex_Digit_Display hex_digit_display_8 (.value(LedData[3:0]));  // open: dp
  Multiplexer #(.width(5), .enable("false")) multiplexer_1 (
    .in0(if_id_1_ir_2[25:21]), .in1(5'b00010), .out(id_r1_num), .sel(syscall));
  Multiplexer #(.width(5), .enable("false")) multiplexer_2 (
    .in0(if_id_1_ir_2[20:16]), .in1(5'b00100), .out(id_r2_num), .sel(syscall));
  \硬布线控制器  \u_硬布线控制器_1  (
    .Func(Func), .OP(OP), .ALU_OP(\硬布线控制器_1_alu_op ), .MemToReg(\硬布线控制器_1_memtoreg ),
    .MemWrite(\硬布线控制器_1_memwrite ), .ALU_SRC(\硬布线控制器_1_alu_src ), .RegWrite(\硬布线控制器_1_regwrite ),
    .SysCALL(syscall), .SignedExt(\硬布线控制器_1_signedext ), .RegDst(id_regdst), .JR(\硬布线控制器_1_jr ),
    .JMP(\硬布线控制器_1_jmp ), .Beq(\硬布线控制器_1_beq ), .JAL(id_jal), .Bne(\硬布线控制器_1_bne ), .BGTZ(BGTZ), .LH(LH),
    .SRLV(SRLV));
  Multiplexer #(.select(2), .width(5), .enable("false")) multiplexer_3 (
    .in0(if_id_1_ir_2[20:16]), .in1({5{1'b1}}), .in2(if_id_1_ir_2[15:11]), .out(id_w_num),
    .sel({id_regdst, id_jal}));  // open: in3
  and and_7 (still_j, ~ex_prejump, succeed);  // AND_Gate
  or or_4 (succeed, branch, JMP);
  or or_5 (or_5_out, JMP, ex_cj);
  // Probe on \总周期数 
  // Probe on \无条件分支数 
  // Probe on \条件分支成功数 
  // Probe on \LoadUse次数 
  and and_8 (pre_bubble, ex_prejump, ~succeed);  // AND_Gate
  and and_9 (and_9_out, succeed, ~if_prejump, ex_prejump);  // AND_Gate
  Adder #(.width(32)) adder_1 (.a(32'h4), .b(EX_PC), .out(adder_1_out));  // open: cin, cout
  \load_use检测  \load_use检测_1  (
    .EX_load(ex_load), .load_use(load_use), .OP(OP), .EX_WriteReg_num(ex_w_num), .EX_RegWrite(ex_regwrite),
    .MEM_WriteReg_num(mem_w_num), .MEM_RegWrite(mem_regwrite), .sel_a(sel_a_id), .Func(Func),
    .ID_R1_num(id_r1_num), .ID_R2_num(id_r2_num), .sel_b(sel_b_id), .mem_load(mem_load));
  // Probe on IF_PC[11:0]
  // RegisterFile registerfile_1: pin names not known; wires that end beside it: Reg_din, CLK, WB_RegWrite, W_num, id_r1_num, id_r2_num, registerfile_1_p7, registerfile_1_p8, registerfile_1_p9
  assign PC = pre_bubble ? adder_2_out : 32'bz;  // Controlled_Buffer controlled_buffer_1
  Adder #(.width(32)) adder_2 (.a(32'h4), .b(EX_PC), .out(adder_2_out));  // open: cin, cout
  and and_10 (and_10_out, ~pre_bubble, if_prejump);  // AND_Gate
  and and_11 (and_11_out, or_5_out, ex_miss);
  and and_12 (and_12_out, or_5_out, ~ex_miss);  // AND_Gate
  // Probe on ID_PC[11:0]
  not not_2 (not_2_out, en);
  ID_EX id_ex_1 (
    .MemtoReg(\硬布线控制器_1_memtoreg ), .RegWrite(\硬布线控制器_1_regwrite ), .jal(id_jal), .CLK(CLK),
    .W_num(id_w_num), .JMP(\硬布线控制器_1_jmp ), .JR(\硬布线控制器_1_jr ), .MemWrite(\硬布线控制器_1_memwrite ),
    .Syscall(syscall), .ALUOP(\硬布线控制器_1_alu_op ), .AluSrcB(\硬布线控制器_1_alu_src ),
    .SignExt(\硬布线控制器_1_signedext ), .IR({OP, if_id_1_ir_2, Func}), .PC(ID_PC), .A(registerfile_1_p7),
    .B(registerfile_1_p8), .MemToReg_2(id_ex_1_memtoreg_2), .RegWrite_2(ex_regwrite), .jal_2(id_ex_1_jal_2),
    .W_num_2(ex_w_num), .JMP_2(JMP), .JR_2(JR), .MemWrite_2(id_ex_1_memwrite_2), .Syscall_2(syscall_ex),
    .ALUOP_2(id_ex_1_aluop_2), .AluSrcB_2(AluSrcB), .SignExt_2(SignedExt),
    .IR_2({id_ex_1_ir_2, instr_index, imme}), .PC_2(EX_PC), .A_2(R1), .B_2(R2), .\使能端_低电平正常工作 (not_2_out),
    .\同步清零_气泡_高电平有效 (or_3_out), .beq(\硬布线控制器_1_beq ), .bne(\硬布线控制器_1_bne ), .beq_2(id_ex_1_beq_2),
    .bne_2(id_ex_1_bne_2), .bgtz(BGTZ), .bgtz_2(bgtz_ex), .lh(LH), .lh_2(id_ex_1_lh_2), .srlv(SRLV),
    .srlv_2(registerfile_1_p9), .sel_a(sel_a_id), .sel_a_2(sel_a), .sel_b(sel_b_id), .sel_b_2(sel_b),
    .miss(id_miss), .miss_2(ex_miss), .prejump(id_prejump), .prejump_2(ex_prejump), .hit_num(id_hitnum),
    .hit_num_2(ex_hitnum));
  or or_6 (ex_cj, id_ex_1_bne_2, bgtz_ex, id_ex_1_beq_2);
  assign PC = and_10_out ? jumpaddr : 32'bz;  // Controlled_Buffer controlled_buffer_2
  assign bit_extender_1_out = {{14{imme[15]}}, {imme, 2'b00}};  // Bit_Extender bit_extender_1
  Multiplexer #(.select(2), .width(32), .enable("false")) multiplexer_4 (
    .in0(R2), .in1(MEM_alu), .in2(wb_alu), .in3(wb_dout), .out(show_data), .sel(sel_b));
  // Probe on EX_PC[11:0]
  // Probe on MEM_PC[11:0]
  MIPS_ALU mips_alu_1 (
    .X(multi_A), .Y(B), .AluOP(id_ex_1_aluop_2), .Equal(sel), .Result(mips_alu_1_result),
    .shamt(multiplexer_5_out));  // open: Result_2
  Multiplexer #(.width(5), .enable("false")) multiplexer_5 (
    .in0(imme[10:6]), .in1(multi_A[4:0]), .out(multiplexer_5_out), .sel(registerfile_1_p9));
  Comparator #(.width(32), .mode("unsigned")) comparator_1 (
    .a({32{1'b0}}), .b(multi_A), .eq(comparator_1_eq));  // open: gt, lt
  Adder #(.width(32)) adder_3 (.a(32'h4), .b(IF_PC), .out(adder_3_out));  // open: cin, cout
  assign PC = and_9_out ? adder_3_out : 32'bz;  // Controlled_Buffer controlled_buffer_3
  assign bht_load = and_11_out ? 1'b1 : 1'bz;  // Controlled_Buffer controlled_buffer_4
  not not_3 (not_3_out, and_11_out);
  Multiplexer #(.width(2), .enable("false")) multiplexer_6 (
    .in0(2'b11), .in1(2'b00), .out(multiplexer_6_out), .sel(ex_cj));
  assign bht_update = and_12_out ? 1'b1 : 1'bz;  // Controlled_Buffer controlled_buffer_5
  not not_4 (not_4_out, and_12_out);
  Adder #(.width(32)) adder_4 (.a(adder_1_out), .b(bit_extender_1_out), .out(adder_4_out));  // open: cin, cout
  Adder #(.width(32)) adder_5 (.a(32'h4), .b(IF_PC), .out(adder_5_out));  // open: cin, cout
  Multiplexer #(.width(32), .enable("false")) multiplexer_7 (
    .in0({adder_1_out[31:28], instr_index, imme, 2'b00}), .in1(multi_A), .out(multiplexer_7_out), .sel(JR));
  assign bit_extender_2_out = {{16{imme[15]}}, imme};  // Bit_Extender bit_extender_2
  assign bit_extender_3_out = {{16{1'b0}}, imme};  // Bit_Extender bit_extender_3
  assign B = and_13_out ? show_data : 32'bz;  // Controlled_Buffer controlled_buffer_6
  and and_13 (and_13_out, ~syscall_ex, ~AluSrcB);  // AND_Gate
  // Probe on WB_PC[11:0]
  or or_7 (ex_load, id_ex_1_lh_2, id_ex_1_memtoreg_2);
  and and_14 (and_14_out, id_ex_1_beq_2, sel);
  and and_15 (and_15_out, ~sel, id_ex_1_bne_2);  // AND_Gate
  and and_16 (and_16_out, bgtz_ex, ~multi_A[31], ~comparator_1_eq);  // AND_Gate
  nor nor_1 (nor_1_out, and_10_out, and_9_out, pre_bubble);
  assign bht_load = not_3_out ? 1'b0 : 1'bz;  // Controlled_Buffer controlled_buffer_7
  assign initial_state = and_11_out ? multiplexer_6_out : 2'bz;  // Controlled_Buffer controlled_buffer_8
  assign bht_update = not_4_out ? 1'b0 : 1'bz;  // Controlled_Buffer controlled_buffer_9
  Multiplexer #(.width(32), .enable("false")) multiplexer_8 (
    .in0(adder_5_out), .in1(adder_4_out), .out(multiplexer_8_out), .sel(branch));
  assign no_pre_PC = JMP ? multiplexer_7_out : 32'bz;  // Controlled_Buffer controlled_buffer_10
  assign B = syscall_ex ? 32'h22 : 32'bz;  // Controlled_Buffer controlled_buffer_11
  assign B = SignedExt ? bit_extender_2_out : 32'bz;  // Controlled_Buffer controlled_buffer_12
  assign B = and_17_out ? bit_extender_3_out : 32'bz;  // Controlled_Buffer controlled_buffer_13
  and and_17 (and_17_out, AluSrcB, ~SignedExt);  // AND_Gate
  not not_5 (not_5_out, en);
  EX_MEM ex_mem_1 (
    .MemtoReg(id_ex_1_memtoreg_2), .RegWrite(ex_regwrite), .jal(id_ex_1_jal_2), .CLK(CLK), .lh(id_ex_1_lh_2),
    .MemWrite(id_ex_1_memwrite_2), .pause(pause), .IR({id_ex_1_ir_2, instr_index, imme}), .PC(EX_PC),
    .ALU_Result(mips_alu_1_result), .MemToReg_2(ex_mem_1_memtoreg_2), .RegWrite_2(mem_regwrite),
    .jal_2(ex_mem_1_jal_2), .lh_2(LH_MEM), .MemWrite_2(ex_mem_1_memwrite_2), .pause_2(ex_mem_1_pause_2),
    .IR_2(ex_mem_1_ir_2), .PC_2(MEM_PC), .ALU_Result_2(MEM_alu), .\使能端_低电平正常工作 (not_5_out), .B(show_data),
    .B_2(ex_mem_1_b_2), .\同步清零_气泡_高电平有效 (RST), .W_num(ex_w_num), .W_num_2(mem_w_num));
  or or_8 (branch, and_14_out, and_16_out, and_15_out);
  assign PC = nor_1_out ? no_pre_PC : 32'bz;  // Controlled_Buffer controlled_buffer_14
  assign no_pre_PC = not_6_out ? multiplexer_8_out : 32'bz;  // Controlled_Buffer controlled_buffer_15
  not not_6 (not_6_out, JMP);
  or or_9 (bubble_1, pre_bubble, still_j);
  Multiplexer #(.select(2), .width(32), .enable("false")) multiplexer_9 (
    .in0(R1), .in1(MEM_alu), .in2(wb_alu), .in3(wb_dout), .out(multi_A), .sel(sel_a));
  or or_10 (bubble_2, bubble_1, load_use);
  // MIPS_RAM mips_ram_1: pin names not known; wires that end beside it: MEM_alu[21:0], MEM_alu[21:2], ex_mem_1_b_2, ex_mem_1_memwrite_2, CLK, mem_load, RST, mips_ram_1_p8
  or or_11 (mem_load, ex_mem_1_memtoreg_2, LH_MEM);
  assign controlled_buffer_16_out = ex_mem_1_memtoreg_2 ? mips_ram_1_p8 : 32'bz;  // Controlled_Buffer controlled_buffer_16
  or or_12 (or_12_out, bubble_1, load_use);
  not not_7 (not_7_out, en);
  MEM_WB mem_wb_1 (
    .MemtoReg(mem_load), .RegWrite(mem_regwrite), .jal(ex_mem_1_jal_2), .CLK(CLK), .pause(ex_mem_1_pause_2),
    .IR(ex_mem_1_ir_2), .PC(MEM_PC), .ALU_Result(MEM_alu), .MemToReg_2(mem_wb_1_memtoreg_2),
    .RegWrite_2(WB_RegWrite), .jal_2(jal), .pause_2(wb_pause), .IR_2({mem_wb_1_ir_2, wb_imme}), .PC_2(WB_PC),
    .ALU_Result_2(wb_alu), .Dout(controlled_buffer_16_out), .Dout_2(wb_dout), .\同步清零_气泡_高电平有效 (RST),
    .\使能端_低电平正常工作 (not_7_out), .W_num(mem_w_num), .W_num_2(W_num));
  assign bit_extender_4_out = {{16{mips_ram_1_p8[15]}}, mips_ram_1_p8[15:0]};  // Bit_Extender bit_extender_4
  assign bit_extender_5_out = {{16{mips_ram_1_p8[31]}}, mips_ram_1_p8[31:16]};  // Bit_Extender bit_extender_5
  Counter #(.width(16), .max('hffff)) counter_5 (
    .count(or_12_out), .Q(\插入气泡数 ), .clk(CLK), .clr(RST));  // open: load, D, carry
  Multiplexer #(.width(32), .enable("false")) multiplexer_10 (
    .in0(bit_extender_4_out), .in1(bit_extender_5_out), .out(multiplexer_10_out), .sel(MEM_alu[1]));
  assign controlled_buffer_16_out = LH_MEM ? multiplexer_10_out : 32'bz;  // Controlled_Buffer controlled_buffer_17
  Adder #(.width(32)) adder_6 (.a(32'h4), .b(WB_PC), .out(adder_6_out));  // open: cin, cout
  nor nor_2 (nor_2_out, mem_wb_1_memtoreg_2, jal);
  assign Reg_din = jal ? adder_6_out : 32'bz;  // Controlled_Buffer controlled_buffer_18
  assign Reg_din = mem_wb_1_memtoreg_2 ? wb_dout : 32'bz;  // Controlled_Buffer controlled_buffer_19
  assign Reg_din = nor_2_out ? wb_alu : 32'bz;  // Controlled_Buffer controlled_buffer_20

  // Other names for the same wires on the sheet: instr_index[15:0] = imme; shamt[4:0] = imme[10:6]

  // Notes on the sheet:
  //   中断源
  //   中断等待指示
  //   指令存储器
  //   数码管输出
  //   contents of rom_1 (hex, n*v repeats v):
  //   20110001 8000c05 20110001 20120002 20130003 8000c09 20110001 20120002 20130003 8000c0d 20110001
  //   20120002 20130003 8000c11 20110001 20120002 20130003 c000cf9 20100001 20110001 118fc0 112020
  //   20020022 c 118882 12200001 8000c15 112020 20020022 c 20110001 118880 112020 20020022 c 12200001
  //   8000c1f 20110001 118fc0 112020 20020022 c 1188c3 112020 20020022 c 118903 112020 20020022 c 118903
  //   112020 20020022 c 118903 112020 20020022 c 118903 112020 20020022 c 118903 112020 20020022 c 118903
  //   112020 20020022 c 118903 112020 20020022 c 20100001 109fc0 139fc3 8021 2012000c 24160003 26100001
  //   3210000f 20080008 20090001 139900 2709825 132020 20020022 c 1094022 1500fff9 22100001 2018000f
  //   2188024 108700 20080008 20090001 139902 2709825 132021 20020022 c 1094022 1500fff9 108702 2c9b022
  //   12c00001 8000c50 4020 1084027 84400 3508ffff 82021 20020022 c 2010ffff 20110000 ae300000 22100001
  //   22310004 ae300000 22100001 22310004 ae300000 22100001 22310004 ae300000 22100001 22310004 ae300000
  //   22100001 22310004 ae300000 22100001 22310004 ae300000 22100001 22310004 ae300000 22100001 22310004
  //   ae300000 22100001 22310004 ae300000 22100001 22310004 ae300000 22100001 22310004 ae300000 22100001
  //   22310004 ae300000 22100001 22310004 ae300000 22100001 22310004 ae300000 22100001 22310004 ae300000
  //   22100001 22310004 22100001 8020 2011003c 8e130000 8e340000 274402a 11000002 ae330000 ae140000
  //   2231fffc 1611fff8 102020 20020022 c 22100004 2011003c 1611fff2 20020032 c 20080001 20090003 20110876
  //   118d00 112020 20020022 c 200b0008 1118806 1318806 112020 20020022 c 216bffff 1560fff9 2002000a c
  //   2008ffff 20117777 112020 20020022 c 200b0010 3a31ffff 112020 20020022 c 216bffff 1560fffa 2002000a c
  //   20090000 200b0010 34118483 20120404 118c00 129400 36318281 22520404 ad310000 2328820 21290004
  //   216bffff 1560fffb 200b0020 20090000 85310000 112020 20020022 c 21290002 216bffff 1560fff9 2002000a c
  //   2011000f 112020 20020022 c 2231ffff 1e20fffb 2002000a c 2002000a c 20100000 22100001 102020 20020022
  //   c 22100002 102020 20020022 c 22100003 102020 20020022 c 22100004 102020 20020022 c 22100005 102020
  //   20020022 c 22100006 102020 20020022 c 22100007 102020 20020022 c 22100008 102020 20020022 20020022 c
  //   3e00008
  //   rs
  //   rt
  //   rd
  //   流水调试日志用
  //   ins_ind
  //   分支气泡
  //   数据气泡
endmodule

module BHT (
  input  [31:0] Addr,
  input  [31:0] BlockDataIn,
  input  BlkDataReady,
  input  CLK,
  input  stateReady,
  input  succeed,
  input  [1:0] initial_state,
  input  ex_Miss,
  input  [7:0] update_num,
  input  [31:0] load_pc,
  output Miss,
  output [31:0] DataOut,
  output pre_jump,
  output [7:0] hit_num
);

  wire and_1_out, and_2_out, and_3_out, and_4_out, and_5_out, and_6_out, and_7_out, and_8_out, and_9_out,
       and_10_out, and_11_out, and_12_out, and_13_out, and_14_out, and_15_out, and_17_out, and_18_out,
       and_19_out, and_20_out, and_21_out, and_22_out, and_23_out, and_24_out, and_25_out, comparator_1_eq,
       comparator_2_eq, comparator_3_eq, comparator_4_eq, comparator_5_eq, comparator_6_eq, comparator_7_eq,
       comparator_8_eq, demultiplexer_1_out0, demultiplexer_1_out1, demultiplexer_1_out2,
       demultiplexer_1_out3, demultiplexer_1_out4, demultiplexer_1_out5, demultiplexer_1_out6,
       demultiplexer_1_out7, L0, L1, L2, L3, L4, L5, L6, L7, max3_1_p5, max3_1_p6, max3_2_p5, max3_2_p6,
       max3_3_p4, max3_3_p5, max3_4_p6, max3_4_p7, max3_5_p5, max3_5_p6, max3_6_p5, max3_6_p6, not_1_out,
       not_2_out, not_4_out, or_1_out, or_2_out, or_3_out, or_4_out, or_5_out, or_6_out, or_7_out, or_8_out,
       or_9_out, or_10_out, or_11_out, or_12_out, or_13_out, or_14_out, or_15_out, or_16_out, or_17_out, U0,
       U1, U2, U3, U4, U5, U6, U7, V0, V1, V2, V3, V4, V5, V6, V7, warm;
  wire [0:0] pre_state;
  wire [1:0] fsm_state, next_state, register_17_q, register_18_q, register_19_q, register_20_q,
       register_21_q, register_22_q, register_23_q, register_24_q, state;
  wire [2:0] num;
  wire [15:0] C0, C1, C2, C3, C4, C5, C6, C7;
  wire [31:0] register_25_q, register_26_q, register_27_q, register_28_q, register_29_q, register_30_q,
       register_31_q, register_32_q, Tag0, Tag1, Tag2, Tag3, Tag4, Tag5, Tag6, Tag7;

  FSM fsm_1 (.in_1(state), .in_2(succeed), .out_3(fsm_state));
  Register #(.width(1)) register_1 (.D(1'b1), .en(and_1_out), .Q(V0), .clk(CLK));  // open: clr
  and and_1 (and_1_out, L0, BlkDataReady, 1'b1);
  Register #(.width(1)) register_2 (.D(1'b1), .en(and_2_out), .Q(V1), .clk(CLK));  // open: clr
  and and_2 (and_2_out, 1'b1, BlkDataReady, L1);
  and and_3 (and_3_out, 1'b1, BlkDataReady, L2);
  Register #(.width(1)) register_3 (.D(1'b1), .en(and_4_out), .Q(V3), .clk(CLK));  // open: clr
  and and_4 (and_4_out, 1'b1, BlkDataReady, L3);
  Register #(.width(1)) register_4 (.D(1'b1), .en(and_5_out), .Q(V4), .clk(CLK));  // open: clr
  and and_5 (and_5_out, 1'b1, BlkDataReady, L4);
  and and_6 (and_6_out, 1'b1, BlkDataReady, L5);
  Register #(.width(1)) register_5 (.D(1'b1), .en(and_7_out), .Q(V6), .clk(CLK));  // open: clr
  and and_7 (and_7_out, 1'b1, BlkDataReady, L6);
  Register #(.width(1)) register_6 (.D(1'b1), .en(and_8_out), .Q(V7), .clk(CLK));  // open: clr
  and and_8 (and_8_out, 1'b1, BlkDataReady, L7);
  Register #(.width(1)) register_7 (.D(1'b1), .en(and_3_out), .Q(V2), .clk(CLK));  // open: clr
  Register #(.width(1)) register_8 (.D(1'b1), .en(and_6_out), .Q(V5), .clk(CLK));  // open: clr
  // Max3 max3_1: pin names not known; wires that end beside it: C0, 3'b000, C1, 3'b001, max3_1_p5, max3_1_p6
  // Max3 max3_2: pin names not known; wires that end beside it: C2, 3'b010, C3, 3'b011, max3_2_p5, max3_2_p6
  // Max3 max3_3: pin names not known; wires that end beside it: C4, 3'b100, C5, max3_3_p4, max3_3_p5
  // Max3 max3_4: pin names not known; wires that end beside it: 3'b101, C6, 3'b110, C7, 3'b111, max3_4_p6, max3_4_p7
  assign L0 = ex_Miss ? not_1_out : 1'bz;  // Controlled_Buffer controlled_buffer_1
  not not_1 (not_1_out, V0);
  and and_9 (and_9_out, ~V1, ~L0);  // AND_Gate
  assign L1 = ex_Miss ? and_9_out : 1'bz;  // Controlled_Buffer controlled_buffer_2
  and and_10 (and_10_out, ~L0, ~L1, ~V2);  // AND_Gate
  assign L2 = ex_Miss ? and_10_out : 1'bz;  // Controlled_Buffer controlled_buffer_3
  and and_11 (and_11_out, ~L0, ~L1, ~L2, ~V3);  // AND_Gate
  assign L3 = ex_Miss ? and_11_out : 1'bz;  // Controlled_Buffer controlled_buffer_4
  assign L4 = ex_Miss ? and_12_out : 1'bz;  // Controlled_Buffer controlled_buffer_5
  and and_12 (and_12_out, ~L0, ~L1, ~L2, ~L3, ~V4);  // AND_Gate
  and and_13 (and_13_out, ~L0, ~L1, ~L2, ~L3, ~L4, ~V5);  // AND_Gate
  assign L5 = ex_Miss ? and_13_out : 1'bz;  // Controlled_Buffer controlled_buffer_6
  assign L6 = ex_Miss ? and_14_out : 1'bz;  // Controlled_Buffer controlled_buffer_7
  and and_14 (and_14_out, ~L0, ~L1, ~L2, ~L3, ~L4, ~L5, ~V6);  // AND_Gate
  and and_15 (and_15_out, ~L0, ~L1, ~L2, ~L3, ~L4, ~L5, ~L6, ~V7);  // AND_Gate
  assign L7 = ex_Miss ? and_15_out : 1'bz;  // Controlled_Buffer controlled_buffer_8
  Register #(.width(32)) register_9 (.D(load_pc), .en(and_1_out), .Q(Tag0), .clk(CLK));  // open: clr
  Register #(.width(32)) register_10 (.D(load_pc), .en(and_2_out), .Q(Tag1), .clk(CLK));  // open: clr
  Register #(.width(32)) register_11 (.D(load_pc), .en(and_4_out), .Q(Tag3), .clk(CLK));  // open: clr
  Register #(.width(32)) register_12 (.D(load_pc), .en(and_5_out), .Q(Tag4), .clk(CLK));  // open: clr
  Register #(.width(32)) register_13 (.D(load_pc), .en(and_7_out), .Q(Tag6), .clk(CLK));  // open: clr
  Register #(.width(32)) register_14 (.D(load_pc), .en(and_8_out), .Q(Tag7), .clk(CLK));  // open: clr
  // Max3 max3_5: pin names not known; wires that end beside it: max3_1_p5, max3_1_p6, max3_2_p5, max3_2_p6, max3_5_p5, max3_5_p6, max3_5_p5
  // Max3 max3_6: pin names not known; wires that end beside it: max3_3_p4, max3_3_p5, max3_4_p6, max3_4_p7, max3_6_p5, max3_6_p6
  Register #(.width(32)) register_15 (.D(load_pc), .en(and_3_out), .Q(Tag2), .clk(CLK));  // open: clr
  Register #(.width(32)) register_16 (.D(load_pc), .en(and_6_out), .Q(Tag5), .clk(CLK));  // open: clr
  // Max3 max3_7: pin names not known; wires that end beside it: max3_5_p6, max3_6_p5, max3_6_p6, num
  assign next_state = stateReady ? fsm_state : 2'bz;  // Controlled_Buffer controlled_buffer_9
  assign next_state = BlkDataReady ? initial_state : 2'bz;  // Controlled_Buffer controlled_buffer_10
  Counter #(.width(16), .max('hffff)) counter_1 (
    .count(1'b1), .Q(C0), .clk(CLK), .clr(or_1_out));  // open: load, D, carry
  or or_1 (or_1_out, and_1_out, and_18_out);
  Counter #(.width(16), .max('hffff)) counter_2 (
    .count(1'b1), .Q(C1), .clk(CLK), .clr(or_2_out));  // open: load, D, carry
  Counter #(.width(16), .max('hffff)) counter_3 (
    .count(1'b1), .Q(C2), .clk(CLK), .clr(or_3_out));  // open: load, D, carry
  Counter #(.width(16), .max('hffff)) counter_4 (
    .count(1'b1), .Q(C3), .clk(CLK), .clr(or_4_out));  // open: load, D, carry
  Counter #(.width(16), .max('hffff)) counter_5 (
    .count(1'b1), .Q(C4), .clk(CLK), .clr(or_5_out));  // open: load, D, carry
  Counter #(.width(16), .max('hffff)) counter_6 (
    .count(1'b1), .Q(C5), .clk(CLK), .clr(or_6_out));  // open: load, D, carry
  Counter #(.width(16), .max('hffff)) counter_7 (
    .count(1'b1), .Q(C6), .clk(CLK), .clr(or_7_out));  // open: load, D, carry
  Counter #(.width(16), .max('hffff)) counter_8 (
    .count(1'b1), .Q(C7), .clk(CLK), .clr(or_8_out));  // open: load, D, carry
  or or_2 (or_2_out, and_2_out, and_19_out);
  or or_3 (or_3_out, and_20_out, and_3_out);
  or or_4 (or_4_out, and_21_out, and_4_out);
  or or_5 (or_5_out, and_5_out, and_22_out);
  or or_6 (or_6_out, and_6_out, and_23_out);
  or or_7 (or_7_out, and_7_out, and_24_out);
  or or_8 (or_8_out, and_8_out, and_25_out);
  Demultiplexer #(.select(3), .enable("false")) demultiplexer_1 (
    .out0(demultiplexer_1_out0), .out1(demultiplexer_1_out1), .out2(demultiplexer_1_out2),
    .out3(demultiplexer_1_out3), .out4(demultiplexer_1_out4), .out5(demultiplexer_1_out5),
    .out6(demultiplexer_1_out6), .out7(demultiplexer_1_out7), .in(1'b1), .sel(num));
  assign L0 = not_2_out ? 1'b0 : 1'bz;  // Controlled_Buffer controlled_buffer_11
  assign L1 = not_2_out ? 1'b0 : 1'bz;  // Controlled_Buffer controlled_buffer_12
  assign L2 = not_2_out ? 1'b0 : 1'bz;  // Controlled_Buffer controlled_buffer_13
  assign L3 = not_2_out ? 1'b0 : 1'bz;  // Controlled_Buffer controlled_buffer_14
  assign L4 = not_2_out ? 1'b0 : 1'bz;  // Controlled_Buffer controlled_buffer_15
  assign L5 = not_2_out ? 1'b0 : 1'bz;  // Controlled_Buffer controlled_buffer_16
  assign L6 = not_2_out ? 1'b0 : 1'bz;  // Controlled_Buffer controlled_buffer_17
  assign L7 = not_2_out ? 1'b0 : 1'bz;  // Controlled_Buffer controlled_buffer_18
  not not_2 (not_2_out, ex_Miss);
  or or_9 (or_9_out, U0, and_1_out);
  or or_10 (or_10_out, U1, and_2_out);
  or or_11 (or_11_out, U2, and_3_out);
  or or_12 (or_12_out, U3, and_4_out);
  or or_13 (or_13_out, U4, and_5_out);
  or or_14 (or_14_out, U5, and_6_out);
  or or_15 (or_15_out, U6, and_7_out);
  or or_16 (or_16_out, U7, and_8_out);
  assign L6 = and_17_out ? demultiplexer_1_out6 : 1'bz;  // Controlled_Buffer controlled_buffer_19
  assign L7 = and_17_out ? demultiplexer_1_out7 : 1'bz;  // Controlled_Buffer controlled_buffer_20
  Register #(.width(2)) register_17 (.D(next_state), .en(or_9_out), .Q(register_17_q), .clk(CLK));  // open: clr
  Register #(.width(2)) register_18 (.D(next_state), .en(or_10_out), .Q(register_18_q), .clk(CLK));  // open: clr
  Register #(.width(2)) register_19 (.D(next_state), .en(or_11_out), .Q(register_19_q), .clk(CLK));  // open: clr
  assign state = U3 ? register_20_q : 2'bz;  // Controlled_Buffer controlled_buffer_21
  Register #(.width(2)) register_20 (.D(next_state), .en(or_12_out), .Q(register_20_q), .clk(CLK));  // open: clr
  Register #(.width(2)) register_21 (.D(next_state), .en(or_13_out), .Q(register_21_q), .clk(CLK));  // open: clr
  assign state = U4 ? register_21_q : 2'bz;  // Controlled_Buffer controlled_buffer_22
  Register #(.width(2)) register_22 (.D(next_state), .en(or_14_out), .Q(register_22_q), .clk(CLK));  // open: clr
  Register #(.width(2)) register_23 (.D(next_state), .en(or_15_out), .Q(register_23_q), .clk(CLK));  // open: clr
  assign state = U7 ? register_24_q : 2'bz;  // Controlled_Buffer controlled_buffer_23
  Register #(.width(2)) register_24 (.D(next_state), .en(or_16_out), .Q(register_24_q), .clk(CLK));  // open: clr
  assign L1 = and_17_out ? demultiplexer_1_out1 : 1'bz;  // Controlled_Buffer controlled_buffer_24
  assign L2 = and_17_out ? demultiplexer_1_out2 : 1'bz;  // Controlled_Buffer controlled_buffer_25
  assign L3 = and_17_out ? demultiplexer_1_out3 : 1'bz;  // Controlled_Buffer controlled_buffer_26
  assign L5 = and_17_out ? demultiplexer_1_out5 : 1'bz;  // Controlled_Buffer controlled_buffer_27
  assign L4 = and_17_out ? demultiplexer_1_out4 : 1'bz;  // Controlled_Buffer controlled_buffer_28
  assign state = U0 ? register_17_q : 2'bz;  // Controlled_Buffer controlled_buffer_29
  assign {pre_jump, pre_state[0]} = and_18_out ? register_17_q : 2'bz;  // Controlled_Buffer controlled_buffer_30
  assign state = U1 ? register_18_q : 2'bz;  // Controlled_Buffer controlled_buffer_31
  assign {pre_jump, pre_state[0]} = and_19_out ? register_18_q : 2'bz;  // Controlled_Buffer controlled_buffer_32
  assign state = U2 ? register_19_q : 2'bz;  // Controlled_Buffer controlled_buffer_33
  assign {pre_jump, pre_state[0]} = and_20_out ? register_19_q : 2'bz;  // Controlled_Buffer controlled_buffer_34
  assign {pre_jump, pre_state[0]} = and_21_out ? register_20_q : 2'bz;  // Controlled_Buffer controlled_buffer_35
  assign {pre_jump, pre_state[0]} = and_22_out ? register_21_q : 2'bz;  // Controlled_Buffer controlled_buffer_36
  assign state = U5 ? register_22_q : 2'bz;  // Controlled_Buffer controlled_buffer_37
  assign {pre_jump, pre_state[0]} = and_23_out ? register_22_q : 2'bz;  // Controlled_Buffer controlled_buffer_38
  assign state = U6 ? register_23_q : 2'bz;  // Controlled_Buffer controlled_buffer_39
  assign {pre_jump, pre_state[0]} = and_24_out ? register_23_q : 2'bz;  // Controlled_Buffer controlled_buffer_40
  assign {pre_jump, pre_state[0]} = and_25_out ? register_24_q : 2'bz;  // Controlled_Buffer controlled_buffer_41
  and and_16 (warm, V0, V1, V2, V3, V4, V5, V6, V7);
  assign L0 = and_17_out ? demultiplexer_1_out0 : 1'bz;  // Controlled_Buffer controlled_buffer_42
  Register #(.width(32)) register_25 (.D(BlockDataIn), .en(and_1_out), .Q(register_25_q), .clk(CLK));  // open: clr
  Register #(.width(32)) register_26 (.D(BlockDataIn), .en(and_2_out), .Q(register_26_q), .clk(CLK));  // open: clr
  Register #(.width(32)) register_27 (.D(BlockDataIn), .en(and_3_out), .Q(register_27_q), .clk(CLK));  // open: clr
  Register #(.width(32)) register_28 (.D(BlockDataIn), .en(and_4_out), .Q(register_28_q), .clk(CLK));  // open: clr
  Register #(.width(32)) register_29 (.D(BlockDataIn), .en(and_5_out), .Q(register_29_q), .clk(CLK));  // open: clr
  Register #(.width(32)) register_30 (.D(BlockDataIn), .en(and_6_out), .Q(register_30_q), .clk(CLK));  // open: clr
  Register #(.width(32)) register_31 (.D(BlockDataIn), .en(and_7_out), .Q(register_31_q), .clk(CLK));  // open: clr
  Register #(.width(32)) register_32 (.D(BlockDataIn), .en(and_8_out), .Q(register_32_q), .clk(CLK));  // open: clr
  and and_17 (and_17_out, ex_Miss, warm);
  assign DataOut = and_18_out ? register_25_q : 32'bz;  // Controlled_Buffer controlled_buffer_43
  and and_18 (and_18_out, 1'b1, hit_num[0]);
  assign DataOut = and_19_out ? register_26_q : 32'bz;  // Controlled_Buffer controlled_buffer_44
  and and_19 (and_19_out, 1'b1, hit_num[1]);
  assign DataOut = and_20_out ? register_27_q : 32'bz;  // Controlled_Buffer controlled_buffer_45
  and and_20 (and_20_out, 1'b1, hit_num[2]);
  assign DataOut = and_21_out ? register_28_q : 32'bz;  // Controlled_Buffer controlled_buffer_46
  and and_21 (and_21_out, 1'b1, hit_num[3]);
  assign DataOut = and_22_out ? register_29_q : 32'bz;  // Controlled_Buffer controlled_buffer_47
  and and_22 (and_22_out, 1'b1, hit_num[4]);
  assign DataOut = and_23_out ? register_30_q : 32'bz;  // Controlled_Buffer controlled_buffer_48
  and and_23 (and_23_out, 1'b1, hit_num[5]);
  assign DataOut = and_24_out ? register_31_q : 32'bz;  // Controlled_Buffer controlled_buffer_49
  and and_24 (and_24_out, 1'b1, hit_num[6]);
  assign DataOut = and_25_out ? register_32_q : 32'bz;  // Controlled_Buffer controlled_buffer_50
  and and_25 (and_25_out, 1'b1, hit_num[7]);
  Comparator #(.width(32)) comparator_1 (.a(Addr), .b(Tag0), .eq(comparator_1_eq));  // open: gt, lt
  Comparator #(.width(32)) comparator_2 (.a(Addr), .b(Tag1), .eq(comparator_2_eq));  // open: gt, lt
  Comparator #(.width(32)) comparator_3 (.a(Addr), .b(Tag2), .eq(comparator_3_eq));  // open: gt, lt
  Comparator #(.width(32)) comparator_4 (.a(Addr), .b(Tag3), .eq(comparator_4_eq));  // open: gt, lt
  Comparator #(.width(32)) comparator_5 (.a(Addr), .b(Tag4), .eq(comparator_5_eq));  // open: gt, lt
  Comparator #(.width(32)) comparator_6 (.a(Addr), .b(Tag5), .eq(comparator_6_eq));  // open: gt, lt
  Comparator #(.width(32)) comparator_7 (.a(Addr), .b(Tag6), .eq(comparator_7_eq));  // open: gt, lt
  Comparator #(.width(32)) comparator_8 (.a(Addr), .b(Tag7), .eq(comparator_8_eq));  // open: gt, lt
  and and_26 (hit_num[0], V0, comparator_1_eq);
  and and_27 (hit_num[1], V1, comparator_2_eq);
  and and_28 (hit_num[2], V2, comparator_3_eq);
  and and_29 (hit_num[3], V3, comparator_4_eq);
  and and_30 (hit_num[4], V4, comparator_5_eq);
  and and_31 (hit_num[5], V5, comparator_6_eq);
  and and_32 (hit_num[6], V6, comparator_7_eq);
  and and_33 (hit_num[7], V7, comparator_8_eq);
  or or_17 (or_17_out, hit_num[7], hit_num[6], hit_num[5], hit_num[4], hit_num[2], hit_num[1], hit_num[0], hit_num[3]);
  not not_3 (Miss, or_17_out);
  not not_4 (not_4_out, stateReady);
  assign state = not_4_out ? 2'b00 : 2'bz;  // Controlled_Buffer controlled_buffer_51
  assign {pre_jump, pre_state[0]} = Miss ? 2'b00 : 2'bz;  // Controlled_Buffer controlled_buffer_52
  and and_34 (U0, stateReady, update_num[0]);
  and and_35 (U1, update_num[1], stateReady);
  and and_36 (U2, stateReady, update_num[2]);
  and and_37 (U3, update_num[3], stateReady);
  and and_38 (U4, stateReady, update_num[4]);
  and and_39 (U5, stateReady, update_num[5]);
  and and_40 (U6, update_num[6], stateReady);
  and and_41 (U7, stateReady, update_num[7]);

  // Other names for the same wires on the sheet: Blk[31:0] = BlockDataIn; BlkReady = BlkDataReady;
  //   find_pc[31:0] = Addr; hit0 = hit_num[0]; hit1 = hit_num[1]; hit2 = hit_num[2]; hit3 = hit_num[3];
  //   hit4 = hit_num[4]; hit5 = hit_num[5]; hit6 = hit_num[6]; hit7 = hit_num[7]; pre_state[1] = pre_jump;
  //   SlotData[31:0] = DataOut; tag[31:0] = load_pc

  // Notes on the sheet:
  //   输入引脚区
  //   有空位时给出第一个空位信号
  //   hit了不需要load
  //   输出引脚区
  //   warm=1 无空位要淘汰
  //   无空位时淘汰
endmodule

module FSM (
  input  [1:0] in_1,
  input  in_2,
  output [1:0] out_3
);

  wire and_1_out, and_2_out, and_3_out, and_4_out, demultiplexer_1_out0, demultiplexer_1_out2;

  Demultiplexer #(.select(2), .disabled(0), .enable("false")) demultiplexer_1 (
    .out0(demultiplexer_1_out0), .out2(demultiplexer_1_out2), .in(1'b1), .sel(in_1));  // open: out1, out3
  and and_1 (and_1_out, ~demultiplexer_1_out2, ~in_2);  // AND_Gate
  and and_2 (and_2_out, demultiplexer_1_out2, ~in_2);  // AND_Gate
  assign out_3 = and_1_out ? 2'b00 : 2'bz;  // Controlled_Buffer controlled_buffer_1
  assign out_3 = and_2_out ? 2'b11 : 2'bz;  // Controlled_Buffer controlled_buffer_2
  and and_3 (and_3_out, demultiplexer_1_out0, in_2);
  assign out_3 = and_3_out ? 2'b01 : 2'bz;  // Controlled_Buffer controlled_buffer_3
  and and_4 (and_4_out, in_2, ~demultiplexer_1_out0);  // AND_Gate
  assign out_3 = and_4_out ? 2'b10 : 2'bz;  // Controlled_Buffer controlled_buffer_4

  // Other names for the same wires on the sheet: input_state[1:0] = in_1; output_state[1:0] = out_3; success = in_2
endmodule
