// Logisim project cpu28_interrupt.circ as structural Verilog: 5 circuits, main circuit ◇单级中断
// ALU
module MIPS_ALU (
  input  [4:0] shamt,
  input  [31:0] X,
  input  [31:0] Y,
  input  [3:0] AluOP,
  output Equal,
  output [31:0] Result,
  output [31:0] Result_2
);

  wire [0:0] comparator_1_lt, comparator_2_lt;
  wire [31:0] adder_1_out, AND_out, divider_1_out, divider_1_rem, multiplier_1_cout, multiplier_1_out,
       NOR_out, OR_out, shifter_1_out, shifter_2_out, shifter_3_out, subtractor_1_out, XOR_out;

  assign AND_out = X & Y;  // AND_Gate AND, 32 bits wide
  assign OR_out = X | Y;  // OR_Gate OR, 32 bits wide
  Shifter #(.width(32)) shifter_1 (.in(Y), .\dist (shamt), .out(shifter_1_out));
  Shifter #(.width(32), .shift("ar")) shifter_2 (.in(Y), .\dist (shamt), .out(shifter_2_out));
  Shifter #(.width(32), .shift("lr")) shifter_3 (.in(Y), .\dist (shamt), .out(shifter_3_out));
  Multiplier #(.width(32)) multiplier_1 (.a(X), .b(Y), .out(multiplier_1_out), .cout(multiplier_1_cout));  // open: cin
  Divider #(.width(32)) divider_1 (.a(X), .b(Y), .out(divider_1_out), .rem(divider_1_rem));  // open: upper
  Adder #(.width(32)) adder_1 (.a(X), .b(Y), .out(adder_1_out));  // open: cin, cout
  Subtractor #(.width(32)) subtractor_1 (.a(X), .b(Y), .out(subtractor_1_out));  // open: bin, bout
  assign XOR_out = X ^ Y;  // XOR_Gate XOR, 32 bits wide
  assign NOR_out = ~(X | Y);  // NOR_Gate NOR, 32 bits wide
  Comparator #(.width(32)) comparator_1 (.a(X), .b(Y), .eq(Equal), .lt(comparator_1_lt[0]));  // open: gt
  Comparator #(.width(32), .mode("unsigned")) comparator_2 (.a(X), .b(Y), .lt(comparator_2_lt[0]));  // open: gt, eq
  Multiplexer #(.select(4), .width(32), .enable("false")) multiplexer_1 (
    .in0(shifter_1_out), .in1(shifter_2_out), .in2(shifter_3_out), .in3(multiplier_1_out),
    .in4(divider_1_out), .in5(adder_1_out), .in6(subtractor_1_out), .in7(AND_out), .in8(OR_out),
    .in9(XOR_out), .in10(NOR_out), .in11({{31{1'b0}}, comparator_1_lt[0]}),
    .in12({{31{1'b0}}, comparator_2_lt[0]}), .in13({32{1'b0}}), .in14({32{1'b0}}), .in15({32{1'b0}}),
    .out(Result), .sel(AluOP));
  Multiplexer #(.select(4), .width(32), .enable("false")) multiplexer_2 (
    .in0({32{1'b0}}), .in1({32{1'b0}}), .in2({32{1'b0}}), .in3(multiplier_1_cout), .in4(divider_1_rem),
    .in5({32{1'b0}}), .in6({32{1'b0}}), .in7({32{1'b0}}), .in8({32{1'b0}}), .in9({32{1'b0}}),
    .in10({32{1'b0}}), .in11({32{1'b0}}), .in12({32{1'b0}}), .in13({32{1'b0}}), .in14({32{1'b0}}),
    .in15({32{1'b0}}), .out(Result_2), .sel(AluOP));

  // Other names for the same wires on the sheet: Result2[31:0] = Result_2; S[3:0] = AluOP

  // Notes on the sheet:
  //   不要改变此引脚区域内容，也不要改变ALU封装形式
  //   输入引脚
  //   输出引脚
endmodule

module MIPS_Regifile (
  input  [31:0] Din,
  input  Clk,
  input  WE,
  input  [4:0] R1_num,
  input  [4:0] W_num,
  input  [4:0] R2_num,
  output [31:0] R1,
  output [31:0] R2
);

  // RegisterFile registerfile_1: pin names not known; wires that end beside it: Din, Clk, WE, W_num, R1_num, R2_num, R1, R2
endmodule

// 源寄存器使用情况
module \源寄存器使用情况  (
  input  OP0,
  input  OP1,
  input  OP2,
  input  OP3,
  input  OP4,
  input  OP5,
  input  F0,
  input  F1,
  input  F2,
  input  F3,
  input  F4,
  input  F5,
  output R1_Used,
  output R2_Used
);
endmodule

module \数据相关检测  (
  input  [5:0] OP,
  input  [4:0] EX_WriteReg_num,
  input  EX_RegWrite,
  input  [4:0] MEM_WriteReg_num,
  input  MEM_RegWrite,
  input  [5:0] Func,
  input  [4:0] ID_R1_num,
  input  [4:0] ID_R2_num,
  output \数据相关 
);

  wire \源寄存器使用情况_1_r1_used , \源寄存器使用情况_1_r2_used ;

  \源寄存器使用情况  \u_源寄存器使用情况_1  (
    .OP0(OP[0]), .OP1(OP[1]), .OP2(OP[2]), .OP3(OP[3]), .OP4(OP[4]), .OP5(OP[5]), .F0(Func[0]), .F1(Func[1]),
    .F2(Func[2]), .F3(Func[3]), .F4(Func[4]), .F5(Func[5]), .R1_Used(\源寄存器使用情况_1_r1_used ),
    .R2_Used(\源寄存器使用情况_1_r2_used ));

  // Other names for the same wires on the sheet: OP_CODE[5:0] = OP
endmodule

module \单级中断  (
);

  wire AluSrcB, and_1_out, and_2_out, and_3_out, and_4_out, and_5_out, and_8_out, and_11_out, and_12_out,
       and_13_out, and_14_out, and_15_out, and_16_out, and_17_out, and_18_out, and_19_out, and_20_out, BGTZ,
       CJ, CLK, clr_1, clr_2, clr_3, comparator_1_eq, cop0, counter_3_q, d_ff_1_q, d_ff_2_q, d_ff_3_q,
       d_ff_4_q, d_ff_5_q, d_ff_6_q, demultiplexer_2_out0, demultiplexer_2_out1, demultiplexer_2_out2, eret,
       Go, IE, IE_in, \int , interrupt, IR1, IR2, IR3, jal, JMP, JR, LH, LW, mfc0, mtc0, not_2_out, nothalt,
       or_4_out, or_5_out, or_6_out, or_7_out, or_8_out, or_9_out, or_10_out, or_12_out, regdst,
       register_5_q, RST, sel, SignedExt, SRLV, syscall, W1, W2, W3, \硬布线控制器_1_beq , \硬布线控制器_1_bne ,
       \硬布线控制器_1_memwrite , \硬布线控制器_1_regwrite ;
  wire [0:0] mips_alu_1_result_2;
  wire [1:0] inter_num, num, register_3_q;
  wire [3:0] multiplexer_7_out, \硬布线控制器_1_alu_op ;
  wire [4:0] multiplexer_3_out, multiplexer_4_out, multiplexer_6_out, W_num;
  wire [11:0] EX_PC, ID_PC, IF_PC, MEM_PC, WB_PC;
  wire [15:0] imme, \LoadUse次数 , \总周期数 , \插入气泡数 , \无条件分支数 , \条件分支成功数 ;
  wire [25:16] instr_index;
  wire [31:0] adder_1_out, adder_2_out, B, bit_extender_1_out, bit_extender_2_out, bit_extender_3_out,
       bit_extender_4_out, bit_extender_5_out, Din, EPC, LedData, mips_alu_1_result, mips_ram_1_p9,
       multiplexer_2_out, multiplexer_5_out, multiplexer_8_out, PC, PC_ori, PC_q, R2, registerfile_1_p7;
  wire [31:26] rom_1_data;

  Button \u_总复位  (.out(RST));
  Button _1 (.out(IR1));
  Button _2 (.out(IR2));
  Button _3 (.out(IR3));
  Button \u_继续运行  (.out(Go));
  LED led_1 (.in(W1));
  LED led_2 (.in(W2));
  LED led_3 (.in(W3));
  and and_1 (and_1_out, nothalt, JMP);
  Register #(.width(32)) u_PC (.D(PC), .en(nothalt), .Q(PC_q), .clk(CLK), .clr(RST));
  or or_1 (W1, d_ff_4_q, d_ff_1_q);
  or or_2 (W2, d_ff_5_q, d_ff_2_q);
  or or_3 (W3, d_ff_6_q, d_ff_3_q);
  and and_2 (and_2_out, sel, syscall);
  Hex_Digit_Display hex_digit_display_1 (.value(LedData[31:28]));  // open: dp
  Counter #(.width(16), .max('hffff)) counter_1 (
    .count(and_1_out), .Q(\无条件分支数 ), .clk(CLK), .clr(RST));  // open: load, D, carry
  Counter #(.width(16), .max('hffff)) counter_2 (
    .count(nothalt), .Q(\总周期数 ), .clk(CLK), .clr(RST));  // open: load, D, carry
  Adder #(.width(32)) adder_1 (.a(PC_q), .b(32'h4), .out(adder_1_out));  // open: cin, cout
  assign IE_in = or_4_out ? 1'b1 : 1'bz;  // Controlled_Buffer controlled_buffer_1
  assign IE_in = mtc0 ? 1'b0 : 1'bz;  // Controlled_Buffer controlled_buffer_2
  or or_4 (or_4_out, mfc0, eret);
  D_Flip_Flop #(.trigger("high")) d_ff_1 (.clk(IR1), .D(1'b1), .Q(d_ff_1_q), .reset(d_ff_4_q));  // open: Qn, preset, en
  D_Flip_Flop #(.trigger("high")) d_ff_2 (.clk(IR2), .D(1'b1), .Q(d_ff_2_q), .reset(d_ff_5_q));  // open: Qn, preset, en
  D_Flip_Flop #(.trigger("high")) d_ff_3 (.clk(IR3), .D(1'b1), .Q(d_ff_3_q), .reset(d_ff_6_q));  // open: Qn, preset, en
  Register #(.width(32)) register_1 (.D(R2), .en(and_2_out), .Q(LedData), .clk(CLK));  // open: clr
  Multiplexer #(.select(2), .width(5), .enable("false")) multiplexer_1 (
    .in0(instr_index[20:16]), .in1({5{1'b1}}), .in2(imme[15:11]), .out(W_num), .sel({regdst, jal}));  // open: in3
  Hex_Digit_Display hex_digit_display_2 (.value(LedData[23:20]));  // open: dp
  Hex_Digit_Display hex_digit_display_3 (.value(LedData[27:24]));  // open: dp
  assign bit_extender_1_out = {{14{imme[15]}}, {imme, 2'b00}};  // Bit_Extender bit_extender_1
  or or_5 (or_5_out, d_ff_1_q, d_ff_4_q);
  or or_6 (or_6_out, d_ff_2_q, d_ff_5_q);
  and and_3 (and_3_out, or_6_out, ~clr_2);  // AND_Gate
  or or_7 (or_7_out, d_ff_3_q, d_ff_6_q);
  and and_4 (and_4_out, or_7_out, ~clr_3);  // AND_Gate
  or or_8 (or_8_out, Go, and_5_out);
  and and_5 (and_5_out, ~sel, syscall);  // AND_Gate
  Hex_Digit_Display hex_digit_display_4 (.value(LedData[19:16]));  // open: dp
  Hex_Digit_Display hex_digit_display_5 (.value(LedData[15:12]));  // open: dp
  and and_6 (mtc0, instr_index[23], ~instr_index[25], cop0);  // AND_Gate
  and and_7 (eret, cop0, instr_index[25]);
  ROM #(.addrWidth(10), .dataWidth(32)) rom_1 (.addr(PC_q[11:2]), .data({rom_1_data, instr_index, imme}));  // open: sel
  Adder #(.width(32)) adder_2 (.a(adder_1_out), .b(bit_extender_1_out), .out(adder_2_out));  // open: cin, cout
  D_Flip_Flop #(.trigger("high")) d_ff_4 (.clk(CLK), .D(and_8_out), .Q(d_ff_4_q));  // open: Qn, preset, en, reset
  and and_8 (and_8_out, or_5_out, ~clr_1);  // AND_Gate
  D_Flip_Flop #(.trigger("high")) d_ff_5 (.clk(CLK), .D(and_3_out), .Q(d_ff_5_q));  // open: Qn, preset, en, reset
  D_Flip_Flop #(.trigger("high")) d_ff_6 (.clk(CLK), .D(and_4_out), .Q(d_ff_6_q));  // open: Qn, preset, en, reset
  Counter #(.width(1), .max('h1)) counter_3 (
    .count(or_8_out), .Q(counter_3_q), .clk(CLK), .clr(RST));  // open: load, D, carry
  not not_1 (nothalt, counter_3_q);
  Hex_Digit_Display hex_digit_display_6 (.value(LedData[7:4]));  // open: dp
  Hex_Digit_Display hex_digit_display_7 (.value(LedData[11:8]));  // open: dp
  Clock clock_1 (.out(CLK));
  and and_9 (mfc0, ~instr_index[25], ~instr_index[23], cop0);  // AND_Gate
  Multiplexer #(.width(32), .enable("false")) multiplexer_2 (
    .in0(adder_1_out), .in1(adder_2_out), .out(multiplexer_2_out), .sel(CJ));
  Hex_Digit_Display hex_digit_display_8 (.value(LedData[3:0]));  // open: dp
  \硬布线控制器  \u_硬布线控制器_1  (
    .Func(imme[5:0]), .OP(rom_1_data), .ALU_OP(\硬布线控制器_1_alu_op ), .MemToReg(LW),
    .MemWrite(\硬布线控制器_1_memwrite ), .ALU_SRC(AluSrcB), .RegWrite(\硬布线控制器_1_regwrite ), .SysCALL(syscall),
    .SignedExt(SignedExt), .RegDst(regdst), .JR(JR), .JMP(JMP), .Beq(\硬布线控制器_1_beq ), .JAL(jal),
    .Bne(\硬布线控制器_1_bne ), .BGTZ(BGTZ), .LH(LH), .SRLV(SRLV), .cop0(cop0));
  Multiplexer #(.width(5), .enable("false")) multiplexer_3 (
    .in0(instr_index[25:21]), .in1(5'b00010), .out(multiplexer_3_out), .sel(syscall));
  Multiplexer #(.width(5), .enable("false")) multiplexer_4 (
    .in0(instr_index[20:16]), .in1(5'b00100), .out(multiplexer_4_out), .sel(syscall));
  Priority_Encoder #(.select(2)) priority_encoder_1 (
    .in0(d_ff_4_q), .in1(d_ff_5_q), .in2(d_ff_6_q), .out(num));  // open: in3, gs, en_out, en_in
  // Probe on num
  Register #(.width(2)) register_2 (.D(num), .en(IE), .Q(inter_num), .clk(CLK));  // open: clr
  or or_9 (or_9_out, d_ff_4_q, d_ff_5_q, d_ff_6_q);
  and and_10 (interrupt, or_9_out, IE);
  D_Flip_Flop d_ff_7 (.clk(CLK), .D(IE_in), .Q(IE), .en(cop0));  // open: Qn, preset, reset
  Demultiplexer #(.select(2), .disabled(0)) demultiplexer_1 (
    .out0(clr_1), .out1(clr_2), .out2(clr_3), .in(1'b1), .sel(register_3_q), .en(and_11_out));  // open: out3
  and and_11 (and_11_out, cop0, eret);
  Register #(.width(2)) register_3 (.D(inter_num), .Q(register_3_q), .clk(CLK));  // open: en, clr
  Demultiplexer #(.select(2), .disabled(0)) demultiplexer_2 (
    .out0(demultiplexer_2_out0), .out1(demultiplexer_2_out1), .out2(demultiplexer_2_out2), .in(1'b1),
    .sel(num), .en(and_12_out));  // open: out3
  and and_12 (and_12_out, \int , ~eret);  // AND_Gate
  // Probe on \总周期数 
  // Probe on \无条件分支数 
  // Probe on \条件分支成功数 
  // Probe on \插入气泡数 
  // Probe on \LoadUse次数 
  Register #(.width(32)) register_4 (.D(PC_ori), .en(\int ), .Q(EPC), .clk(CLK));  // open: clr
  assign PC = demultiplexer_2_out0 ? 32'h120 : 32'bz;  // Controlled_Buffer controlled_buffer_3
  // Probe on IF_PC
  // RegisterFile registerfile_1: pin names not known; wires that end beside it: Din, CLK, \硬布线控制器_1_regwrite , W_num, multiplexer_3_out, multiplexer_4_out, registerfile_1_p7, R2
  assign PC_ori = JMP ? multiplexer_5_out : 32'bz;  // Controlled_Buffer controlled_buffer_4
  Multiplexer #(.width(32), .enable("false")) multiplexer_5 (
    .in0({adder_1_out[31:28], instr_index, imme, 2'b00}), .in1(registerfile_1_p7), .out(multiplexer_5_out),
    .sel(JR));
  D_Flip_Flop d_ff_8 (.clk(interrupt), .D(1'b1), .Q(\int ), .reset(register_5_q));  // open: Qn, preset, en
  or or_10 (or_10_out, \int , register_5_q);
  assign PC = demultiplexer_2_out1 ? 32'h1d4 : 32'bz;  // Controlled_Buffer controlled_buffer_5
  assign PC = demultiplexer_2_out2 ? 32'h288 : 32'bz;  // Controlled_Buffer controlled_buffer_6
  assign PC = eret ? EPC : 32'bz;  // Controlled_Buffer controlled_buffer_7
  // Probe on ID_PC
  Comparator #(.width(32), .mode("unsigned")) comparator_1 (
    .a({32{1'b0}}), .b(registerfile_1_p7), .eq(comparator_1_eq));  // open: gt, lt
  Multiplexer #(.width(5), .enable("false")) multiplexer_6 (
    .in0(imme[10:6]), .in1(registerfile_1_p7[4:0]), .out(multiplexer_6_out), .sel(SRLV));
  assign PC_ori = not_2_out ? multiplexer_2_out : 32'bz;  // Controlled_Buffer controlled_buffer_8
  not not_2 (not_2_out, JMP);
  Register #(.width(1)) register_5 (.D(or_10_out), .Q(register_5_q), .clk(CLK), .clr(eret));  // open: en
  assign PC = and_13_out ? PC_ori : 32'bz;  // Controlled_Buffer controlled_buffer_9
  and and_13 (and_13_out, ~\int , ~eret);  // AND_Gate
  // Probe on MEM_PC
  // Probe on EX_PC
  and and_14 (and_14_out, \硬布线控制器_1_beq , sel);
  and and_15 (and_15_out, BGTZ, ~registerfile_1_p7[31], ~comparator_1_eq);  // AND_Gate
  cpu28_simplified_changed_controller__MIPS_ALU mips_alu_1 (
    .X(registerfile_1_p7), .Y(B), .AluOP(\硬布线控制器_1_alu_op ), .Equal(sel),
    .Result({mips_alu_1_result[31:2], mips_alu_1_result_2[0], mips_alu_1_result[0]}),
    .shamt(multiplexer_6_out));  // open: Result_2
  assign bit_extender_2_out = {{16{imme[15]}}, imme};  // Bit_Extender bit_extender_2
  assign bit_extender_3_out = {{16{1'b0}}, imme};  // Bit_Extender bit_extender_3
  assign B = and_16_out ? R2 : 32'bz;  // Controlled_Buffer controlled_buffer_10
  and and_16 (and_16_out, ~syscall, ~AluSrcB);  // AND_Gate
  // Probe on WB_PC
  or or_11 (CJ, and_14_out, and_15_out, and_17_out);
  and and_17 (and_17_out, \硬布线控制器_1_bne , ~sel);  // AND_Gate
  assign Din = jal ? adder_1_out : 32'bz;  // Controlled_Buffer controlled_buffer_11
  assign B = syscall ? 32'h22 : 32'bz;  // Controlled_Buffer controlled_buffer_12
  assign B = SignedExt ? bit_extender_2_out : 32'bz;  // Controlled_Buffer controlled_buffer_13
  assign B = and_18_out ? bit_extender_3_out : 32'bz;  // Controlled_Buffer controlled_buffer_14
  and and_18 (and_18_out, AluSrcB, ~SignedExt);  // AND_Gate
  or or_12 (or_12_out, LW, LH);
  Multiplexer #(.select(2), .width(4), .enable("false")) multiplexer_7 (
    .in0(4'b1111), .in1(4'b1111), .in2(4'b0011), .in3(4'b1100), .out(multiplexer_7_out),
    .sel({LH, mips_alu_1_result_2[0]}));
  and and_19 (and_19_out, ~LW, ~LH, ~jal);  // AND_Gate
  // MIPS_RAM mips_ram_1: pin names not known; wires that end beside it: {mips_alu_1_result[21:2], mips_alu_1_result_2[0], mips_alu_1_result[0]}, mips_alu_1_result[21:2], R2, \硬布线控制器_1_memwrite , multiplexer_7_out, CLK, or_12_out, RST, mips_ram_1_p9
  assign Din = LW ? mips_ram_1_p9 : 32'bz;  // Controlled_Buffer controlled_buffer_15
  assign Din = and_19_out ? {mips_alu_1_result[31:2], mips_alu_1_result_2[0], mips_alu_1_result[0]} : 32'bz;  // Controlled_Buffer controlled_buffer_16
  assign bit_extender_4_out = {{16{mips_ram_1_p9[15]}}, mips_ram_1_p9[15:0]};  // Bit_Extender bit_extender_4
  assign bit_extender_5_out = {{16{mips_ram_1_p9[31]}}, mips_ram_1_p9[31:16]};  // Bit_Extender bit_extender_5
  Multiplexer #(.width(32), .enable("false")) multiplexer_8 (
    .in0(bit_extender_4_out), .in1(bit_extender_5_out), .out(multiplexer_8_out), .sel(mips_alu_1_result_2[0]));
  assign Din = LH ? multiplexer_8_out : 32'bz;  // Controlled_Buffer controlled_buffer_17
  and and_20 (and_20_out, nothalt, CJ);
  Counter #(.width(16), .max('hffff)) counter_4 (
    .count(and_20_out), .Q(\条件分支成功数 ), .clk(CLK), .clr(RST));  // open: load, D, carry

  // Other names for the same wires on the sheet: instr_index[15:0] = imme; sham[4:0] = imme[10:6];
  //   rd[4:0] = imme[15:11]; rt[4:0] = instr_index[20:16]

  // Notes on the sheet:
  //   中断源
  //   中断等待指示
  //   指令存储器
  //   数码管输出
  //   指令字
  //   contents of rom_1 (hex, n*v repeats v):
  //   40090800 20110200 20020022 112020 c 2231ffff 1620fffc 20020032 c 20080001 20090003 20110876 118d00
  //   112020 20020022 c 200b0008 1118806 1318806 112020 20020022 c 216bffff 1560fff9 2002000a c 2008ffff
  //   20117777 112020 20020022 c 200b0010 3a31ffff 112020 20020022 c 216bffff 1560fffa 2002000a c 20090000
  //   200b0010 34118483 20120404 118c00 129400 36318281 22520404 ad310000 2328820 21290004 216bffff
  //   1560fffb 200b0020 20090000 85310000 112020 20020022 c 21290002 216bffff 1560fff9 2002000a c 2011000f
  //   112020 20020022 c 2231ffff 1e20fffb 2002000a c 40910000 ac1d0230 201d0080 27bdfffc afa40000 27bdfffc
  //   afa20000 27bdfffc afb30000 27bdfffc afb40000 27bdfffc afb50000 27bdfffc afb60000 27bdfffc afb00000
  //   20160001 20140006 20150001 168020 108100 2149825 132020 20020022 c 1600fffa 295a022 1680fff7
  //   8fb00000 27bd0004 8fb60000 27bd0004 8fb50000 27bd0004 8fb40000 27bd0004 8fb30000 27bd0004 8fa20000
  //   27bd0004 8fa40000 27bd0004 8c1d0230 42000018 40910000 ac1d0244 201d0100 27bdfffc afa40000 27bdfffc
  //   afa20000 27bdfffc afb30000 27bdfffc afb40000 27bdfffc afb50000 27bdfffc afb60000 27bdfffc afb00000
  //   20160002 20140006 20150001 168020 108100 2149825 132020 20020022 c 1600fffa 295a022 1680fff7
  //   8fb00000 27bd0004 8fb60000 27bd0004 8fb50000 27bd0004 8fb40000 27bd0004 8fb30000 27bd0004 8fa20000
  //   27bd0004 8fa40000 27bd0004 8c1d0244 42000018 40910000 ac1d0258 201d0200 27bdfffc afa40000 27bdfffc
  //   afa20000 27bdfffc afb30000 27bdfffc afb40000 27bdfffc afb50000 27bdfffc afb60000 27bdfffc afb00000
  //   20160003 20140006 20150001 168020 108100 2149825 132020 20020022 c 1600fffa 295a022 1680fff7
  //   8fb00000 27bd0004 8fb60000 27bd0004 8fb50000 27bd0004 8fb40000 27bd0004 8fb30000 27bd0004 8fa20000
  //   27bd0004 8fa40000 27bd0004 8fa40000 8c1d0258 42000018
  //   JMP
  //   JR
  //   OP
  //   Func
  //   OP
  //   Func
  //   rs
  //   rt
  //   rd
  //   shamt
  //   imme
  //   ins_ind
  //   Beq
  //   Bne
  //   MemToReg
  //   MemWrite
  //   AluOP
  //   AluSrcB
  //   RegWrite
  //   JAL
  //   RegDst
  //   Syscall
  //   流水调试日志用
endmodule
